// Logisim project full_processorv2.circ as structural Verilog: 19 circuits, main circuit full_processor
// and
module bitwise_and (
  input  [31:0] in_1,
  input  [31:0] Input_A,
  output [31:0] out_3
);

  and and_1 (out_3[0], Input_A[0], in_1[0]);
  and and_2 (out_3[1], Input_A[1], in_1[1]);
  and and_3 (out_3[2], Input_A[2], in_1[2]);
  and and_4 (out_3[3], Input_A[3], in_1[3]);
  and and_5 (out_3[4], Input_A[4], in_1[4]);
  and and_6 (out_3[5], Input_A[5], in_1[5]);
  and and_7 (out_3[6], Input_A[6], in_1[6]);
  and and_8 (out_3[7], Input_A[7], in_1[7]);
  and and_9 (out_3[8], Input_A[8], in_1[8]);
  and and_10 (out_3[9], Input_A[9], in_1[9]);
  and and_11 (out_3[10], Input_A[10], in_1[10]);
  and and_12 (out_3[11], Input_A[11], in_1[11]);
  and and_13 (out_3[12], Input_A[12], in_1[12]);
  and and_14 (out_3[13], Input_A[13], in_1[13]);
  and and_15 (out_3[14], Input_A[14], in_1[14]);
  and and_16 (out_3[15], Input_A[15], in_1[15]);
  and and_17 (out_3[16], Input_A[16], in_1[16]);
  and and_18 (out_3[17], Input_A[17], in_1[17]);
  and and_19 (out_3[18], Input_A[18], in_1[18]);
  and and_20 (out_3[19], Input_A[19], in_1[19]);
  and and_21 (out_3[20], Input_A[20], in_1[20]);
  and and_22 (out_3[21], Input_A[21], in_1[21]);
  and and_23 (out_3[22], Input_A[22], in_1[22]);
  and and_24 (out_3[23], Input_A[23], in_1[23]);
  and and_25 (out_3[24], Input_A[24], in_1[24]);
  and and_26 (out_3[25], Input_A[25], in_1[25]);
  and and_27 (out_3[26], Input_A[26], in_1[26]);
  and and_28 (out_3[27], Input_A[27], in_1[27]);
  and and_29 (out_3[28], Input_A[28], in_1[28]);
  and and_30 (out_3[29], Input_A[29], in_1[29]);
  and and_31 (out_3[30], Input_A[30], in_1[30]);
  and and_32 (out_3[31], Input_A[31], in_1[31]);
endmodule

// or
module bitwise_or (
  input  [31:0] in_1,
  input  [31:0] Input_A,
  output [31:0] out_3
);

  or or_1 (out_3[0], Input_A[0], in_1[0]);
  or or_2 (out_3[1], Input_A[1], in_1[1]);
  or or_3 (out_3[2], Input_A[2], in_1[2]);
  or or_4 (out_3[3], Input_A[3], in_1[3]);
  or or_5 (out_3[4], Input_A[4], in_1[4]);
  or or_6 (out_3[5], Input_A[5], in_1[5]);
  or or_7 (out_3[6], Input_A[6], in_1[6]);
  or or_8 (out_3[7], Input_A[7], in_1[7]);
  or or_9 (out_3[8], Input_A[8], in_1[8]);
  or or_10 (out_3[9], Input_A[9], in_1[9]);
  or or_11 (out_3[10], Input_A[10], in_1[10]);
  or or_12 (out_3[11], Input_A[11], in_1[11]);
  or or_13 (out_3[12], Input_A[12], in_1[12]);
  or or_14 (out_3[13], Input_A[13], in_1[13]);
  or or_15 (out_3[14], Input_A[14], in_1[14]);
  or or_16 (out_3[15], Input_A[15], in_1[15]);
  or or_17 (out_3[16], Input_A[16], in_1[16]);
  or or_18 (out_3[17], Input_A[17], in_1[17]);
  or or_19 (out_3[18], Input_A[18], in_1[18]);
  or or_20 (out_3[19], Input_A[19], in_1[19]);
  or or_21 (out_3[20], Input_A[20], in_1[20]);
  or or_22 (out_3[21], Input_A[21], in_1[21]);
  or or_23 (out_3[22], Input_A[22], in_1[22]);
  or or_24 (out_3[23], Input_A[23], in_1[23]);
  or or_25 (out_3[24], Input_A[24], in_1[24]);
  or or_26 (out_3[25], Input_A[25], in_1[25]);
  or or_27 (out_3[26], Input_A[26], in_1[26]);
  or or_28 (out_3[27], Input_A[27], in_1[27]);
  or or_29 (out_3[28], Input_A[28], in_1[28]);
  or or_30 (out_3[29], Input_A[29], in_1[29]);
  or or_31 (out_3[30], Input_A[30], in_1[30]);
  or or_32 (out_3[31], Input_A[31], in_1[31]);
endmodule

module _8_bit_carry_lookahead (
  input  [7:0] A,
  input  [7:0] B,
  input  Cin0,
  output [7:0] out_4,
  output P0,
  output G0,
  output ovf
);

  wire and_1_out, and_2_out, and_3_out, and_4_out, and_5_out, and_6_out, and_7_out, and_8_out, and_9_out,
       and_10_out, and_11_out, and_12_out, and_13_out, and_14_out, and_15_out, and_16_out, and_17_out,
       and_18_out, and_19_out, and_20_out, and_21_out, and_22_out, and_23_out, and_24_out, and_25_out,
       and_26_out, and_27_out, and_28_out, and_29_out, Cout1_out, Cout2_out, Cout3_out, Cout4_out, Cout5_out,
       Cout6_out, g0_t, g1, g2, g3, g4, g5, g6, g7, p0_t, p0c0_out, p1, p1g0_out, p1p0c0_out, p2, p2g1_out,
       p2p1g0_out, p2p1p0c0_out, p3, p4, p5, p6, p7;

  xor S7 (out_4[7], p7, ovf);
  and and_1 (and_1_out, p6, g5);
  and and_2 (and_2_out, p6, p5, g4);
  or Cout7 (ovf, g6, and_1_out, and_2_out, and_3_out, and_4_out, and_5_out, and_6_out, and_7_out);
  and and_3 (and_3_out, p6, p5, p4, g3);
  and and_4 (and_4_out, p6, p5, p4, p3, g2);
  and and_5 (and_5_out, p6, p5, p4, p3, p2, g1);
  and and_6 (and_6_out, p6, p5, p4, p3, p2, p1, g0_t);
  and and_7 (and_7_out, p6, p5, p4, p3, p2, p1, p0_t, Cin0);
  xor S6 (out_4[6], p6, Cout6_out);
  and and_8 (and_8_out, p5, g4);
  or Cout6 (Cout6_out, g5, and_8_out, and_10_out, and_9_out, and_11_out, and_12_out, and_13_out);
  and and_9 (and_9_out, p5, p4, p3, g2);
  and and_10 (and_10_out, p5, p4, g3);
  and and_11 (and_11_out, p5, p4, p3, p2, g1);
  and and_12 (and_12_out, p5, p4, p3, p2, p1, g0_t);
  and and_13 (and_13_out, p5, p4, p3, p2, p1, p0_t, Cin0);
  xor S5 (out_4[5], p5, Cout5_out);
  and and_14 (and_14_out, p4, g3);
  and and_15 (and_15_out, p4, p3, g2);
  or Cout5 (Cout5_out, g4, and_14_out, and_15_out, and_17_out, and_16_out, and_18_out);
  and and_16 (and_16_out, p4, p3, p2, p1, g0_t);
  and and_17 (and_17_out, p4, p3, p2, g1);
  and and_18 (and_18_out, p4, p3, p2, p1, p0_t, Cin0);
  and u_g7 (g7, B[7], A[7]);
  xor u_p7 (p7, B[7], A[7]);
  xor S4 (out_4[4], p4, Cout4_out);
  and u_g6 (g6, B[6], A[6]);
  and and_19 (and_19_out, g2, p3);
  or Cout4 (Cout4_out, g3, and_19_out, and_20_out, and_21_out, and_22_out);
  xor u_p6 (p6, B[6], A[6]);
  and and_20 (and_20_out, g1, p2, p3);
  and and_21 (and_21_out, g0_t, p1, p2, p3);
  xor u_p5 (p5, B[5], A[5]);
  and u_g5 (g5, B[5], A[5]);
  and and_22 (and_22_out, Cin0, p0_t, p1, p2, p3);
  and u_g4 (g4, B[4], A[4]);
  xor S3 (out_4[3], p3, Cout3_out);
  xor u_p4 (p4, B[4], A[4]);
  and p2g1 (p2g1_out, p2, g1);
  or Cout3 (Cout3_out, g2, p2g1_out, p2p1g0_out, p2p1p0c0_out);
  and u_g3 (g3, B[3], A[3]);
  and p2p1g0 (p2p1g0_out, p2, p1, g0_t);
  and p2p1p0c0 (p2p1p0c0_out, p2, p1, p0_t, Cin0);
  xor u_p3 (p3, B[3], A[3]);
  xor S2 (out_4[2], p2, Cout2_out);
  xor u_p2 (p2, B[2], A[2]);
  and u_g2 (g2, B[2], A[2]);
  and p1g0 (p1g0_out, p1, g0_t);
  or Cout2 (Cout2_out, g1, p1g0_out, p1p0c0_out);
  and u_g1 (g1, B[1], A[1]);
  and p1p0c0 (p1p0c0_out, p1, p0_t, Cin0);
  xor u_p1 (p1, B[1], A[1]);
  xor S1 (out_4[1], p1, Cout1_out);
  or Cout1 (Cout1_out, g0_t, p0c0_out);
  and u_g0 (g0_t, B[0], A[0]);
  xor u_p0 (p0_t, B[0], A[0]);
  and p0c0 (p0c0_out, p0_t, Cin0);
  xor S0 (out_4[0], p0_t, Cin0);
  and P0_AND (P0, p0_t, p1, p2, p3, p4, p5, p6, p7);
  and and_23 (and_23_out, p7, g6);
  and and_24 (and_24_out, p7, p6, p5, g4);
  and and_25 (and_25_out, p7, p6, g5);
  or or_1 (G0, g7, and_23_out, and_25_out, and_24_out, and_26_out, and_27_out, and_28_out, and_29_out);
  and and_26 (and_26_out, p7, p6, p5, p4, g3);
  and and_27 (and_27_out, p7, p6, p5, p4, p3, g2);
  and and_28 (and_28_out, p7, p6, p5, p4, p3, p2, g1);
  and and_29 (and_29_out, p7, p6, p5, p4, p3, p2, p1, g0_t);

  // Other names for the same wires on the sheet: result[7:0] = out_4
endmodule

// 32_bit_cla
module _32_bit_carry_lookahead (
  input  [31:0] A_32,
  input  [31:0] B_32,
  input  C0,
  output Overflow,
  output [31:0] S
);

  wire _0_7_g0, _0_7_p0, _8_15_g0, _8_15_p0, _16_23_g0, _16_23_p0, _24_31_g0, _24_31_ovf, _24_31_p0,
       and_1_out, and_2_out, and_3_out, and_4_out, and_5_out, and_6_out, and_7_out, and_8_out, and_9_out,
       and_10_out, C1_out, C2_out, C3_out, C4_out;

  xor xor_1 (Overflow, C4_out, _24_31_ovf);
  and and_1 (and_1_out, _24_31_p0, _16_23_g0);
  or C4 (C4_out, _24_31_g0, and_1_out, and_2_out, and_3_out, and_4_out);
  and and_2 (and_2_out, _24_31_p0, _16_23_p0, _8_15_g0);
  and and_3 (and_3_out, _24_31_p0, _16_23_p0, _8_15_p0, _0_7_g0);
  and and_4 (and_4_out, _24_31_p0, _16_23_p0, _8_15_p0, _0_7_p0, C0);
  _8_bit_carry_lookahead _24_31 (
    .A(A_32[31:24]), .B(B_32[31:24]), .out_4(S[31:24]), .Cin0(C3_out), .P0(_24_31_p0), .G0(_24_31_g0),
    .ovf(_24_31_ovf));
  and and_5 (and_5_out, _0_7_g0, _8_15_p0, _16_23_p0);
  and and_6 (and_6_out, _8_15_g0, _16_23_p0);
  or C3 (C3_out, _16_23_g0, and_6_out, and_5_out, and_7_out);
  and and_7 (and_7_out, _16_23_p0, _8_15_p0, _0_7_p0, C0);
  _8_bit_carry_lookahead _16_23 (
    .A(A_32[23:16]), .B(B_32[23:16]), .out_4(S[23:16]), .Cin0(C2_out), .P0(_16_23_p0), .G0(_16_23_g0));  // open: ovf
  and and_8 (and_8_out, _8_15_p0, _0_7_g0);
  and and_9 (and_9_out, _0_7_p0, _8_15_p0, C0);
  or C2 (C2_out, _8_15_g0, and_8_out, and_9_out);
  _8_bit_carry_lookahead _8_15 (
    .A(A_32[15:8]), .B(B_32[15:8]), .out_4(S[15:8]), .Cin0(C1_out), .P0(_8_15_p0), .G0(_8_15_g0));  // open: ovf
  and and_10 (and_10_out, _0_7_p0, C0);
  or C1 (C1_out, _0_7_g0, and_10_out);
  _8_bit_carry_lookahead _0_7 (
    .A(A_32[7:0]), .B(B_32[7:0]), .out_4(S[7:0]), .Cin0(C0), .P0(_0_7_p0), .G0(_0_7_g0));  // open: ovf

  // Other names for the same wires on the sheet: A1[7:0] = A_32[7:0]; A2[7:0] = A_32[15:8]; A3[7:0] = A_32[23:16];
  //   A4[7:0] = A_32[31:24]; B1[7:0] = B_32[7:0]; B2[7:0] = B_32[15:8]; B3[7:0] = B_32[23:16]; B4[7:0] = B_32[31:24];
  //   S1[7:0] = S[7:0]; S2[7:0] = S[15:8]; S3[7:0] = S[23:16]; S4[7:0] = S[31:24]
endmodule

// NOT
module bitwise_not (
  input  [31:0] Input_B,
  output [31:0] out_2
);

  not not_1 (out_2[0], Input_B[0]);
  not not_2 (out_2[1], Input_B[1]);
  not not_3 (out_2[2], Input_B[2]);
  not not_4 (out_2[3], Input_B[3]);
  not not_5 (out_2[4], Input_B[4]);
  not not_6 (out_2[5], Input_B[5]);
  not not_7 (out_2[6], Input_B[6]);
  not not_8 (out_2[7], Input_B[7]);
  not not_9 (out_2[8], Input_B[8]);
  not not_10 (out_2[9], Input_B[9]);
  not not_11 (out_2[10], Input_B[10]);
  not not_12 (out_2[11], Input_B[11]);
  not not_13 (out_2[12], Input_B[12]);
  not not_14 (out_2[13], Input_B[13]);
  not not_15 (out_2[14], Input_B[14]);
  not not_16 (out_2[15], Input_B[15]);
  not not_17 (out_2[16], Input_B[16]);
  not not_18 (out_2[17], Input_B[17]);
  not not_19 (out_2[18], Input_B[18]);
  not not_20 (out_2[19], Input_B[19]);
  not not_21 (out_2[20], Input_B[20]);
  not not_22 (out_2[21], Input_B[21]);
  not not_23 (out_2[22], Input_B[22]);
  not not_24 (out_2[23], Input_B[23]);
  not not_25 (out_2[24], Input_B[24]);
  not not_26 (out_2[25], Input_B[25]);
  not not_27 (out_2[26], Input_B[26]);
  not not_28 (out_2[27], Input_B[27]);
  not not_29 (out_2[28], Input_B[28]);
  not not_30 (out_2[29], Input_B[29]);
  not not_31 (out_2[30], Input_B[30]);
  not not_32 (out_2[31], Input_B[31]);
endmodule

// sll
module barrell_shifter_SLL (
  input  [31:0] Input,
  input  [4:0] in_2,
  output [31:0] out_3
);

  wire [31:0] multiplexer_1_out, multiplexer_2_out, multiplexer_3_out, multiplexer_4_out;

  Multiplexer #(.width(32), .enable("false")) multiplexer_1 (
    .in0(Input), .in1({Input[15:0], {16{1'b0}}}), .out(multiplexer_1_out), .sel(in_2[4]));
  Multiplexer #(.width(32), .enable("false")) multiplexer_2 (
    .in0(multiplexer_1_out), .in1({multiplexer_1_out[23:0], {8{1'b0}}}), .out(multiplexer_2_out),
    .sel(in_2[3]));
  Multiplexer #(.width(32), .enable("false")) multiplexer_3 (
    .in0(multiplexer_2_out), .in1({multiplexer_2_out[27:0], 4'b0000}), .out(multiplexer_3_out), .sel(in_2[2]));
  Multiplexer #(.width(32), .enable("false")) multiplexer_4 (
    .in0(multiplexer_3_out), .in1({multiplexer_3_out[29:0], 2'b00}), .out(multiplexer_4_out), .sel(in_2[1]));
  Multiplexer #(.width(32), .enable("false")) multiplexer_5 (
    .in0(multiplexer_4_out), .in1({multiplexer_4_out[30:0], 1'b0}), .out(out_3), .sel(in_2[0]));
endmodule

// sra
module barrell_shifter_sra (
  input  [31:0] Input,
  input  [4:0] in_2,
  output [31:0] out_3
);

  wire [31:0] multiplexer_1_out, multiplexer_2_out, multiplexer_3_out, multiplexer_4_out;

  Multiplexer #(.width(32), .enable("false")) multiplexer_1 (
    .in0(Input), .in1({{17{Input[31]}}, Input[30:16]}), .out(multiplexer_1_out), .sel(in_2[4]));
  Multiplexer #(.width(32), .enable("false")) multiplexer_2 (
    .in0(multiplexer_1_out), .in1({{9{multiplexer_1_out[31]}}, multiplexer_1_out[30:8]}),
    .out(multiplexer_2_out), .sel(in_2[3]));
  Multiplexer #(.width(32), .enable("false")) multiplexer_3 (
    .in0(multiplexer_2_out), .in1({{5{multiplexer_2_out[31]}}, multiplexer_2_out[30:4]}),
    .out(multiplexer_3_out), .sel(in_2[2]));
  Multiplexer #(.width(32), .enable("false")) multiplexer_4 (
    .in0(multiplexer_3_out), .in1({{3{multiplexer_3_out[31]}}, multiplexer_3_out[30:2]}),
    .out(multiplexer_4_out), .sel(in_2[1]));
  Multiplexer #(.width(32), .enable("false")) multiplexer_5 (
    .in0(multiplexer_4_out), .in1({{2{multiplexer_4_out[31]}}, multiplexer_4_out[30:1]}), .out(out_3),
    .sel(in_2[0]));
endmodule

module main_alu (
  input  [31:0] InputA,
  input  [31:0] InputB,
  input  [4:0] shift_amt,
  input  [4:0] opcode,
  output [31:0] out_5,
  output overflow,
  output isNotEqual,
  output isLessThan
);

  wire not_1_out, not_2_out, not_3_out, not_4_out, not_5_out, sub;
  wire [31:0] barrell_shifter_sll_1_out_3, barrell_shifter_sra_1_out_3, bitwise_and_1_out_3,
       bitwise_not_1_out_2, bitwise_or_1_out_3, cla_result, multiplexer_1_out;

  bitwise_not bitwise_not_1 (.Input_B(InputB), .out_2(bitwise_not_1_out_2));
  Multiplexer #(.width(32), .enable("false")) multiplexer_1 (
    .in0(InputB), .in1(bitwise_not_1_out_2), .out(multiplexer_1_out), .sel(sub));
  not not_1 (not_1_out, cla_result[31]);
  not not_2 (not_2_out, opcode[3]);
  not not_3 (not_3_out, opcode[1]);
  not not_4 (not_4_out, opcode[4]);
  not not_5 (not_5_out, opcode[2]);
  and and_1 (sub, not_4_out, not_2_out, not_5_out, not_3_out, opcode[0]);
  or or_1 (isNotEqual, cla_result[0], cla_result[1], cla_result[2], cla_result[3], cla_result[4], cla_result[5], cla_result[6], cla_result[7], cla_result[8], cla_result[9], cla_result[10], cla_result[11], cla_result[12], cla_result[13], cla_result[14], cla_result[15], cla_result[16], cla_result[17], cla_result[18], cla_result[19], cla_result[20], cla_result[21], cla_result[22], cla_result[23], cla_result[24], cla_result[25], cla_result[26], cla_result[27], cla_result[28], cla_result[29], cla_result[30], cla_result[31]);
  Multiplexer #(.enable("false")) multiplexer_2 (
    .in0(cla_result[31]), .in1(not_1_out), .out(isLessThan), .sel(overflow));
  _32_bit_carry_lookahead u_32_bit_carry_lookahead_1 (
    .A_32(InputA), .B_32(multiplexer_1_out), .Overflow(overflow), .C0(sub), .S(cla_result));
  bitwise_and bitwise_and_1 (.in_1(InputA), .Input_A(multiplexer_1_out), .out_3(bitwise_and_1_out_3));
  bitwise_or bitwise_or_1 (.in_1(InputA), .Input_A(multiplexer_1_out), .out_3(bitwise_or_1_out_3));
  barrell_shifter_SLL barrell_shifter_sll_1 (.Input(InputA), .out_3(barrell_shifter_sll_1_out_3), .in_2(shift_amt));
  barrell_shifter_sra barrell_shifter_sra_1 (.Input(InputA), .out_3(barrell_shifter_sra_1_out_3), .in_2(shift_amt));
  Multiplexer #(.select(5), .width(32), .enable("false")) multiplexer_3 (
    .in0(cla_result), .in1(cla_result), .in2(bitwise_and_1_out_3), .in3(bitwise_or_1_out_3),
    .in4(barrell_shifter_sll_1_out_3), .in5(barrell_shifter_sra_1_out_3), .out(out_5), .sel(opcode));  // open: in6, in7, in8, in9, in10, in11, in12, in13, in14, in15, in16, in17, in18, in19, in20, in21, in22, in23, in24, in25, in26, in27, in28, in29, in30, in31

  // Other names for the same wires on the sheet: ovf = overflow
endmodule

module register_files (
  input  [31:0] data_writeReg,
  input  clk,
  input  ctrl_reset,
  input  ctrl_writeEnable,
  input  [4:0] ctrl_writeReg,
  input  [4:0] ctrl_readRegA,
  input  [4:0] ctrl_readRegB,
  output [31:0] data_readRegA,
  output [31:0] data_readRegB
);

  wire and_1_out, and_2_out, and_3_out, and_4_out, and_5_out, and_6_out, and_7_out, and_8_out, and_9_out,
       and_10_out, and_11_out, and_12_out, and_13_out, and_14_out, and_15_out, and_16_out, and_17_out,
       and_18_out, and_19_out, and_20_out, and_21_out, and_22_out, and_23_out, and_24_out, and_25_out,
       and_26_out, and_27_out, and_28_out, and_29_out, and_30_out, and_31_out, decoder_1_out1,
       decoder_1_out2, decoder_1_out3, decoder_1_out4, decoder_1_out5, decoder_1_out6, decoder_1_out7,
       decoder_1_out8, decoder_1_out9, decoder_1_out10, decoder_1_out11, decoder_1_out12, decoder_1_out13,
       decoder_1_out14, decoder_1_out15, decoder_1_out16, decoder_1_out17, decoder_1_out18, decoder_1_out19,
       decoder_1_out20, decoder_1_out21, decoder_1_out22, decoder_1_out23, decoder_1_out24, decoder_1_out25,
       decoder_1_out26, decoder_1_out27, decoder_1_out28, decoder_1_out29, decoder_1_out30, decoder_1_out31,
       decoder_2_out0, decoder_2_out1, decoder_2_out2, decoder_2_out3, decoder_2_out4, decoder_2_out5,
       decoder_2_out6, decoder_2_out7, decoder_2_out8, decoder_2_out9, decoder_2_out10, decoder_2_out11,
       decoder_2_out12, decoder_2_out13, decoder_2_out14, decoder_2_out15, decoder_2_out16, decoder_2_out17,
       decoder_2_out18, decoder_2_out19, decoder_2_out20, decoder_2_out21, decoder_2_out22, decoder_2_out23,
       decoder_2_out24, decoder_2_out25, decoder_2_out26, decoder_2_out27, decoder_2_out28, decoder_2_out29,
       decoder_2_out30, decoder_2_out31, decoder_3_out0, decoder_3_out1, decoder_3_out2, decoder_3_out3,
       decoder_3_out4, decoder_3_out5, decoder_3_out6, decoder_3_out7, decoder_3_out8, decoder_3_out9,
       decoder_3_out10, decoder_3_out11, decoder_3_out12, decoder_3_out13, decoder_3_out14, decoder_3_out15,
       decoder_3_out16, decoder_3_out17, decoder_3_out18, decoder_3_out19, decoder_3_out20, decoder_3_out21,
       decoder_3_out22, decoder_3_out23, decoder_3_out24, decoder_3_out25, decoder_3_out26, decoder_3_out27,
       decoder_3_out28, decoder_3_out29, decoder_3_out30, decoder_3_out31;
  wire [31:0] _24_q, reg0, reg1, reg2, reg3, reg4, reg5, reg6, reg7, reg8, reg9, reg10, reg11, reg12, reg13,
       reg14, reg15, reg16, reg17, reg18, reg19, reg20, reg21, reg22, reg23, reg24, reg25, reg26, reg27,
       reg28, reg29, reg30, reg31;

  Decoder #(.select(5), .enable("false")) decoder_1 (
    .out1(decoder_1_out1), .out2(decoder_1_out2), .out3(decoder_1_out3), .out4(decoder_1_out4),
    .out5(decoder_1_out5), .out6(decoder_1_out6), .out7(decoder_1_out7), .out8(decoder_1_out8),
    .out9(decoder_1_out9), .out10(decoder_1_out10), .out11(decoder_1_out11), .out12(decoder_1_out12),
    .out13(decoder_1_out13), .out14(decoder_1_out14), .out15(decoder_1_out15), .out16(decoder_1_out16),
    .out17(decoder_1_out17), .out18(decoder_1_out18), .out19(decoder_1_out19), .out20(decoder_1_out20),
    .out21(decoder_1_out21), .out22(decoder_1_out22), .out23(decoder_1_out23), .out24(decoder_1_out24),
    .out25(decoder_1_out25), .out26(decoder_1_out26), .out27(decoder_1_out27), .out28(decoder_1_out28),
    .out29(decoder_1_out29), .out30(decoder_1_out30), .out31(decoder_1_out31), .sel(ctrl_writeReg));  // open: out0
  Decoder #(.select(5), .enable("false")) decoder_2 (
    .out0(decoder_2_out0), .out1(decoder_2_out1), .out2(decoder_2_out2), .out3(decoder_2_out3),
    .out4(decoder_2_out4), .out5(decoder_2_out5), .out6(decoder_2_out6), .out7(decoder_2_out7),
    .out8(decoder_2_out8), .out9(decoder_2_out9), .out10(decoder_2_out10), .out11(decoder_2_out11),
    .out12(decoder_2_out12), .out13(decoder_2_out13), .out14(decoder_2_out14), .out15(decoder_2_out15),
    .out16(decoder_2_out16), .out17(decoder_2_out17), .out18(decoder_2_out18), .out19(decoder_2_out19),
    .out20(decoder_2_out20), .out21(decoder_2_out21), .out22(decoder_2_out22), .out23(decoder_2_out23),
    .out24(decoder_2_out24), .out25(decoder_2_out25), .out26(decoder_2_out26), .out27(decoder_2_out27),
    .out28(decoder_2_out28), .out29(decoder_2_out29), .out30(decoder_2_out30), .out31(decoder_2_out31),
    .sel(ctrl_readRegA));
  Decoder #(.select(5), .enable("false")) decoder_3 (
    .out0(decoder_3_out0), .out1(decoder_3_out1), .out2(decoder_3_out2), .out3(decoder_3_out3),
    .out4(decoder_3_out4), .out5(decoder_3_out5), .out6(decoder_3_out6), .out7(decoder_3_out7),
    .out8(decoder_3_out8), .out9(decoder_3_out9), .out10(decoder_3_out10), .out11(decoder_3_out11),
    .out12(decoder_3_out12), .out13(decoder_3_out13), .out14(decoder_3_out14), .out15(decoder_3_out15),
    .out16(decoder_3_out16), .out17(decoder_3_out17), .out18(decoder_3_out18), .out19(decoder_3_out19),
    .out20(decoder_3_out20), .out21(decoder_3_out21), .out22(decoder_3_out22), .out23(decoder_3_out23),
    .out24(decoder_3_out24), .out25(decoder_3_out25), .out26(decoder_3_out26), .out27(decoder_3_out27),
    .out28(decoder_3_out28), .out29(decoder_3_out29), .out30(decoder_3_out30), .out31(decoder_3_out31),
    .sel(ctrl_readRegB));
  assign data_readRegA = decoder_2_out0 ? reg0 : 32'bz;  // Controlled_Buffer controlled_buffer_1
  assign data_readRegA = decoder_2_out1 ? reg1 : 32'bz;  // Controlled_Buffer controlled_buffer_2
  assign data_readRegB = decoder_3_out0 ? reg0 : 32'bz;  // Controlled_Buffer controlled_buffer_3
  assign data_readRegB = decoder_3_out1 ? reg1 : 32'bz;  // Controlled_Buffer controlled_buffer_4
  assign data_readRegA = decoder_2_out2 ? reg2 : 32'bz;  // Controlled_Buffer controlled_buffer_5
  assign data_readRegB = decoder_3_out2 ? reg2 : 32'bz;  // Controlled_Buffer controlled_buffer_6
  Register #(.width(32)) _0 (.D(data_writeReg), .en(1'b0), .Q(reg0), .clk(clk), .clr(ctrl_reset));
  Register #(.width(32)) _16 (.D(data_writeReg), .en(and_1_out), .Q(reg16), .clk(clk), .clr(ctrl_reset));
  and and_1 (and_1_out, ctrl_writeEnable, decoder_1_out16);
  assign data_readRegA = decoder_2_out3 ? reg3 : 32'bz;  // Controlled_Buffer controlled_buffer_7
  assign data_readRegA = decoder_2_out4 ? reg4 : 32'bz;  // Controlled_Buffer controlled_buffer_8
  assign data_readRegB = decoder_3_out3 ? reg3 : 32'bz;  // Controlled_Buffer controlled_buffer_9
  assign data_readRegB = decoder_3_out4 ? reg4 : 32'bz;  // Controlled_Buffer controlled_buffer_10
  and and_2 (and_2_out, ctrl_writeEnable, decoder_1_out1);
  and and_3 (and_3_out, ctrl_writeEnable, decoder_1_out17);
  assign data_readRegA = decoder_2_out5 ? reg5 : 32'bz;  // Controlled_Buffer controlled_buffer_11
  assign data_readRegA = decoder_2_out6 ? reg6 : 32'bz;  // Controlled_Buffer controlled_buffer_12
  assign data_readRegB = decoder_3_out5 ? reg5 : 32'bz;  // Controlled_Buffer controlled_buffer_13
  assign data_readRegB = decoder_3_out6 ? reg6 : 32'bz;  // Controlled_Buffer controlled_buffer_14
  Register #(.width(32)) _1 (.D(data_writeReg), .en(and_2_out), .Q(reg1), .clk(clk), .clr(ctrl_reset));
  and and_4 (and_4_out, ctrl_writeEnable, decoder_1_out2);
  Register #(.width(32)) _17 (.D(data_writeReg), .en(and_3_out), .Q(reg17), .clk(clk), .clr(ctrl_reset));
  and and_5 (and_5_out, ctrl_writeEnable, decoder_1_out18);
  assign data_readRegA = decoder_2_out7 ? reg7 : 32'bz;  // Controlled_Buffer controlled_buffer_15
  assign data_readRegB = decoder_3_out7 ? reg7 : 32'bz;  // Controlled_Buffer controlled_buffer_16
  Register #(.width(32)) _2 (.D(data_writeReg), .en(and_4_out), .Q(reg2), .clk(clk), .clr(ctrl_reset));
  Register #(.width(32)) _18 (.D(data_writeReg), .en(and_5_out), .Q(reg18), .clk(clk), .clr(ctrl_reset));
  assign data_readRegA = decoder_2_out8 ? reg8 : 32'bz;  // Controlled_Buffer controlled_buffer_17
  assign data_readRegA = decoder_2_out9 ? reg9 : 32'bz;  // Controlled_Buffer controlled_buffer_18
  assign data_readRegB = decoder_3_out8 ? reg8 : 32'bz;  // Controlled_Buffer controlled_buffer_19
  assign data_readRegB = decoder_3_out9 ? reg9 : 32'bz;  // Controlled_Buffer controlled_buffer_20
  Register #(.width(32)) _3 (.D(data_writeReg), .en(and_6_out), .Q(reg3), .clk(clk), .clr(ctrl_reset));
  and and_6 (and_6_out, ctrl_writeEnable, decoder_1_out3);
  Register #(.width(32)) _19 (.D(data_writeReg), .en(and_7_out), .Q(reg19), .clk(clk), .clr(ctrl_reset));
  and and_7 (and_7_out, ctrl_writeEnable, decoder_1_out19);
  assign data_readRegA = decoder_2_out10 ? reg10 : 32'bz;  // Controlled_Buffer controlled_buffer_21
  assign data_readRegB = decoder_3_out10 ? reg10 : 32'bz;  // Controlled_Buffer controlled_buffer_22
  Register #(.width(32)) _4 (.D(data_writeReg), .en(and_8_out), .Q(reg4), .clk(clk), .clr(ctrl_reset));
  and and_8 (and_8_out, ctrl_writeEnable, decoder_1_out4);
  Register #(.width(32)) _20 (.D(data_writeReg), .en(and_9_out), .Q(reg20), .clk(clk), .clr(ctrl_reset));
  and and_9 (and_9_out, ctrl_writeEnable, decoder_1_out20);
  assign data_readRegA = decoder_2_out11 ? reg11 : 32'bz;  // Controlled_Buffer controlled_buffer_23
  assign data_readRegA = decoder_2_out12 ? reg12 : 32'bz;  // Controlled_Buffer controlled_buffer_24
  assign data_readRegB = decoder_3_out11 ? reg11 : 32'bz;  // Controlled_Buffer controlled_buffer_25
  assign data_readRegB = decoder_3_out12 ? reg12 : 32'bz;  // Controlled_Buffer controlled_buffer_26
  Register #(.width(32)) _5 (.D(data_writeReg), .en(and_10_out), .Q(reg5), .clk(clk), .clr(ctrl_reset));
  and and_10 (and_10_out, ctrl_writeEnable, decoder_1_out5);
  Register #(.width(32)) _21 (.D(data_writeReg), .en(and_11_out), .Q(reg21), .clk(clk), .clr(ctrl_reset));
  and and_11 (and_11_out, ctrl_writeEnable, decoder_1_out21);
  assign data_readRegA = decoder_2_out13 ? reg13 : 32'bz;  // Controlled_Buffer controlled_buffer_27
  assign data_readRegA = decoder_2_out14 ? reg14 : 32'bz;  // Controlled_Buffer controlled_buffer_28
  assign data_readRegB = decoder_3_out13 ? reg13 : 32'bz;  // Controlled_Buffer controlled_buffer_29
  assign data_readRegB = decoder_3_out14 ? reg14 : 32'bz;  // Controlled_Buffer controlled_buffer_30
  Register #(.width(32)) _6 (.D(data_writeReg), .en(and_12_out), .Q(reg6), .clk(clk), .clr(ctrl_reset));
  and and_12 (and_12_out, ctrl_writeEnable, decoder_1_out6);
  Register #(.width(32)) _22 (.D(data_writeReg), .en(and_13_out), .Q(reg22), .clk(clk), .clr(ctrl_reset));
  and and_13 (and_13_out, ctrl_writeEnable, decoder_1_out22);
  assign data_readRegA = decoder_2_out15 ? reg15 : 32'bz;  // Controlled_Buffer controlled_buffer_31
  assign data_readRegB = decoder_3_out15 ? reg15 : 32'bz;  // Controlled_Buffer controlled_buffer_32
  Register #(.width(32)) _7 (.D(data_writeReg), .en(and_14_out), .Q(reg7), .clk(clk), .clr(ctrl_reset));
  and and_14 (and_14_out, ctrl_writeEnable, decoder_1_out7);
  Register #(.width(32)) _23 (.D(data_writeReg), .en(and_15_out), .Q(reg23), .clk(clk), .clr(ctrl_reset));
  and and_15 (and_15_out, ctrl_writeEnable, decoder_1_out23);
  assign data_readRegA = decoder_2_out16 ? reg16 : 32'bz;  // Controlled_Buffer controlled_buffer_33
  assign data_readRegA = decoder_2_out17 ? reg17 : 32'bz;  // Controlled_Buffer controlled_buffer_34
  assign data_readRegB = decoder_3_out16 ? reg16 : 32'bz;  // Controlled_Buffer controlled_buffer_35
  assign data_readRegB = decoder_3_out17 ? reg17 : 32'bz;  // Controlled_Buffer controlled_buffer_36
  Register #(.width(32)) _8 (.D(data_writeReg), .en(and_16_out), .Q(reg8), .clk(clk), .clr(ctrl_reset));
  and and_16 (and_16_out, ctrl_writeEnable, decoder_1_out8);
  Register #(.width(32)) _24 (.D(data_writeReg), .en(and_17_out), .Q(_24_q), .clk(clk), .clr(ctrl_reset));
  and and_17 (and_17_out, ctrl_writeEnable, decoder_1_out24);
  assign data_readRegA = decoder_2_out18 ? reg18 : 32'bz;  // Controlled_Buffer controlled_buffer_37
  assign data_readRegB = decoder_3_out18 ? reg18 : 32'bz;  // Controlled_Buffer controlled_buffer_38
  and and_18 (and_18_out, ctrl_writeEnable, decoder_1_out9);
  and and_19 (and_19_out, ctrl_writeEnable, decoder_1_out25);
  assign data_readRegA = decoder_2_out19 ? reg19 : 32'bz;  // Controlled_Buffer controlled_buffer_39
  assign data_readRegA = decoder_2_out20 ? reg20 : 32'bz;  // Controlled_Buffer controlled_buffer_40
  assign data_readRegB = decoder_3_out19 ? reg19 : 32'bz;  // Controlled_Buffer controlled_buffer_41
  assign data_readRegB = decoder_3_out20 ? reg20 : 32'bz;  // Controlled_Buffer controlled_buffer_42
  Register #(.width(32)) _9 (.D(data_writeReg), .en(and_18_out), .Q(reg9), .clk(clk), .clr(ctrl_reset));
  and and_20 (and_20_out, ctrl_writeEnable, decoder_1_out10);
  Register #(.width(32)) _25 (.D(data_writeReg), .en(and_19_out), .Q(reg25), .clk(clk), .clr(ctrl_reset));
  and and_21 (and_21_out, ctrl_writeEnable, decoder_1_out26);
  assign data_readRegA = decoder_2_out21 ? reg21 : 32'bz;  // Controlled_Buffer controlled_buffer_43
  assign data_readRegA = decoder_2_out22 ? reg22 : 32'bz;  // Controlled_Buffer controlled_buffer_44
  assign data_readRegB = decoder_3_out21 ? reg21 : 32'bz;  // Controlled_Buffer controlled_buffer_45
  assign data_readRegB = decoder_3_out22 ? reg22 : 32'bz;  // Controlled_Buffer controlled_buffer_46
  Register #(.width(32)) _10 (.D(data_writeReg), .en(and_20_out), .Q(reg10), .clk(clk), .clr(ctrl_reset));
  Register #(.width(32)) _26 (.D(data_writeReg), .en(and_21_out), .Q(reg26), .clk(clk), .clr(ctrl_reset));
  assign data_readRegA = decoder_2_out23 ? reg23 : 32'bz;  // Controlled_Buffer controlled_buffer_47
  assign data_readRegB = decoder_3_out23 ? reg23 : 32'bz;  // Controlled_Buffer controlled_buffer_48
  Register #(.width(32)) _11 (.D(data_writeReg), .en(and_22_out), .Q(reg11), .clk(clk), .clr(ctrl_reset));
  and and_22 (and_22_out, ctrl_writeEnable, decoder_1_out11);
  Register #(.width(32)) _27 (.D(data_writeReg), .en(and_23_out), .Q(reg27), .clk(clk), .clr(ctrl_reset));
  and and_23 (and_23_out, ctrl_writeEnable, decoder_1_out27);
  assign data_readRegA = decoder_2_out24 ? reg24 : 32'bz;  // Controlled_Buffer controlled_buffer_49
  assign data_readRegA = decoder_2_out25 ? reg25 : 32'bz;  // Controlled_Buffer controlled_buffer_50
  assign data_readRegB = decoder_3_out24 ? reg24 : 32'bz;  // Controlled_Buffer controlled_buffer_51
  assign data_readRegB = decoder_3_out25 ? reg25 : 32'bz;  // Controlled_Buffer controlled_buffer_52
  Register #(.width(32)) _12 (.D(data_writeReg), .en(and_24_out), .Q(reg12), .clk(clk), .clr(ctrl_reset));
  and and_24 (and_24_out, ctrl_writeEnable, decoder_1_out12);
  Register #(.width(32)) _28 (.D(data_writeReg), .en(and_25_out), .Q(reg28), .clk(clk), .clr(ctrl_reset));
  and and_25 (and_25_out, ctrl_writeEnable, decoder_1_out28);
  assign data_readRegA = decoder_2_out26 ? reg26 : 32'bz;  // Controlled_Buffer controlled_buffer_53
  assign data_readRegB = decoder_3_out26 ? reg26 : 32'bz;  // Controlled_Buffer controlled_buffer_54
  Register #(.width(32)) _13 (.D(data_writeReg), .en(and_26_out), .Q(reg13), .clk(clk), .clr(ctrl_reset));
  and and_26 (and_26_out, ctrl_writeEnable, decoder_1_out13);
  Register #(.width(32)) _29 (.D(data_writeReg), .en(and_27_out), .Q(reg29), .clk(clk), .clr(ctrl_reset));
  and and_27 (and_27_out, ctrl_writeEnable, decoder_1_out29);
  assign data_readRegA = decoder_2_out27 ? reg27 : 32'bz;  // Controlled_Buffer controlled_buffer_55
  assign data_readRegA = decoder_2_out28 ? reg28 : 32'bz;  // Controlled_Buffer controlled_buffer_56
  assign data_readRegB = decoder_3_out27 ? reg27 : 32'bz;  // Controlled_Buffer controlled_buffer_57
  assign data_readRegB = decoder_3_out28 ? reg28 : 32'bz;  // Controlled_Buffer controlled_buffer_58
  Register #(.width(32)) _14 (.D(data_writeReg), .en(and_28_out), .Q(reg14), .clk(clk), .clr(ctrl_reset));
  and and_28 (and_28_out, ctrl_writeEnable, decoder_1_out14);
  Register #(.width(32)) _30 (.D(data_writeReg), .en(and_29_out), .Q(reg30), .clk(clk), .clr(ctrl_reset));
  and and_29 (and_29_out, ctrl_writeEnable, decoder_1_out30);
  assign data_readRegA = decoder_2_out29 ? reg29 : 32'bz;  // Controlled_Buffer controlled_buffer_59
  assign data_readRegA = decoder_2_out30 ? reg30 : 32'bz;  // Controlled_Buffer controlled_buffer_60
  assign data_readRegB = decoder_3_out29 ? reg29 : 32'bz;  // Controlled_Buffer controlled_buffer_61
  assign data_readRegB = decoder_3_out30 ? reg30 : 32'bz;  // Controlled_Buffer controlled_buffer_62
  Register #(.width(32)) _15 (.D(data_writeReg), .en(and_30_out), .Q(reg15), .clk(clk), .clr(ctrl_reset));
  and and_30 (and_30_out, ctrl_writeEnable, decoder_1_out15);
  Register #(.width(32)) _31 (.D(data_writeReg), .en(and_31_out), .Q(reg31), .clk(clk), .clr(ctrl_reset));
  and and_31 (and_31_out, ctrl_writeEnable, decoder_1_out31);
  assign data_readRegA = decoder_2_out31 ? reg31 : 32'bz;  // Controlled_Buffer controlled_buffer_63
  assign data_readRegB = decoder_3_out31 ? reg31 : 32'bz;  // Controlled_Buffer controlled_buffer_64

  // Other names for the same wires on the sheet: reset = ctrl_reset
endmodule

// 8_BIT_CLA
module _8_bit_CLA (
  input  [7:0] A,
  input  [7:0] B,
  input  Cin0,
  output [7:0] out_4,
  output ovf
);

  wire and_1_out, and_2_out, and_3_out, and_4_out, and_5_out, and_6_out, and_7_out, and_8_out, and_9_out,
       and_10_out, and_11_out, and_12_out, and_13_out, and_14_out, and_15_out, and_16_out, and_17_out,
       and_18_out, and_19_out, and_20_out, and_21_out, and_22_out, Cout1_out, Cout2_out, Cout3_out,
       Cout4_out, Cout5_out, Cout6_out, g0, g1, g2, g3, g4, g5, g6, g7, p0, p0c0_out, p1, p1g0_out,
       p1p0c0_out, p2, p2g1_out, p2p1g0_out, p2p1p0c0_out, p3, p4, p5, p6, p7;

  xor S7 (out_4[7], p7, ovf);
  and and_1 (and_1_out, p6, p5, g4);
  and and_2 (and_2_out, p6, g5);
  or Cout7 (ovf, g6, and_2_out, and_1_out, and_4_out, and_3_out, and_5_out, and_6_out, and_7_out);
  and and_3 (and_3_out, p6, p5, p4, p3, g2);
  and and_4 (and_4_out, p6, p5, p4, g3);
  and and_5 (and_5_out, p6, p5, p4, p3, p2, g1);
  and and_6 (and_6_out, p6, p5, p4, p3, p2, p1, g0);
  and and_7 (and_7_out, p6, p5, p4, p3, p2, p1, p0, Cin0);
  xor S6 (out_4[6], p6, Cout6_out);
  and and_8 (and_8_out, p5, g4);
  or Cout6 (Cout6_out, g5, and_8_out, and_9_out, and_10_out, and_11_out, and_12_out, and_13_out);
  and and_9 (and_9_out, p5, p4, g3);
  and and_10 (and_10_out, p5, p4, p3, g2);
  and and_11 (and_11_out, p5, p4, p3, p2, g1);
  and and_12 (and_12_out, p5, p4, p3, p2, p1, g0);
  and and_13 (and_13_out, p5, p4, p3, p2, p1, p0, Cin0);
  xor S5 (out_4[5], p5, Cout5_out);
  and and_14 (and_14_out, p4, g3);
  and and_15 (and_15_out, p4, p3, g2);
  or Cout5 (Cout5_out, g4, and_14_out, and_15_out, and_17_out, and_16_out, and_18_out);
  and and_16 (and_16_out, p4, p3, p2, p1, g0);
  and and_17 (and_17_out, p4, p3, p2, g1);
  and and_18 (and_18_out, p4, p3, p2, p1, p0, Cin0);
  xor u_p7 (p7, B[7], A[7]);
  and u_g7 (g7, B[7], A[7]);
  xor S4 (out_4[4], p4, Cout4_out);
  and u_g6 (g6, B[6], A[6]);
  and and_19 (and_19_out, g2, p3);
  or Cout4 (Cout4_out, g3, and_19_out, and_21_out, and_20_out, and_22_out);
  xor u_p6 (p6, B[6], A[6]);
  and and_20 (and_20_out, g0, p1, p2, p3);
  and and_21 (and_21_out, g1, p2, p3);
  xor u_p5 (p5, B[5], A[5]);
  and u_g5 (g5, B[5], A[5]);
  and and_22 (and_22_out, Cin0, p0, p1, p2, p3);
  and u_g4 (g4, B[4], A[4]);
  xor S3 (out_4[3], p3, Cout3_out);
  xor u_p4 (p4, B[4], A[4]);
  and p2g1 (p2g1_out, p2, g1);
  or Cout3 (Cout3_out, g2, p2g1_out, p2p1g0_out, p2p1p0c0_out);
  and u_g3 (g3, B[3], A[3]);
  and p2p1g0 (p2p1g0_out, p2, p1, g0);
  and p2p1p0c0 (p2p1p0c0_out, p2, p1, p0, Cin0);
  xor u_p3 (p3, B[3], A[3]);
  xor S2 (out_4[2], p2, Cout2_out);
  xor u_p2 (p2, B[2], A[2]);
  and u_g2 (g2, B[2], A[2]);
  and p1g0 (p1g0_out, p1, g0);
  or Cout2 (Cout2_out, g1, p1g0_out, p1p0c0_out);
  and u_g1 (g1, B[1], A[1]);
  and p1p0c0 (p1p0c0_out, p1, p0, Cin0);
  xor u_p1 (p1, B[1], A[1]);
  xor S1 (out_4[1], p1, Cout1_out);
  or Cout1 (Cout1_out, g0, p0c0_out);
  and u_g0 (g0, B[0], A[0]);
  xor u_p0 (p0, B[0], A[0]);
  and p0c0 (p0c0_out, p0, Cin0);
  xor S0 (out_4[0], p0, Cin0);

  // Other names for the same wires on the sheet: result[7:0] = out_4
endmodule

module mdv2 (
  input  [7:0] Multiplicand,
  input  ctrl_div,
  input  [7:0] Multiplier,
  input  Clock,
  input  ctrl_mult,
  output [15:0] data_result,
  output data_resultRDY,
  output ovf_div__mult_in_verilog
);

  wire _1, _2, _2x_out, _4, _8, add2M, addM, and_1_out, and_2_out, and_4_out, Cin_out, d_ff_1_q,
       decoder_1_out0, decoder_1_out1, decoder_1_out2, decoder_1_out5, decoder_1_out6, decoder_1_out7, div0,
       doNothing, FIRST, msb, not_2_out, not_3_out, not_4_out, not_5_out, not_6_out, not_7_out, not_8_out,
       not_9_out, not_10_out, not_11_out, not_12_out, not_13_out, not_14_out, not_15_out, not_16_out,
       not_17_out, not_18_out, not_19_out, not_20_out, not_24_out, not_25_out, or_4_out, or_5_out, or_6_out,
       RDY_div, RDY_mult, sub2M, sub_add, sub_out, subM, xor_1_out;
  wire [0:0] multiplexer_12_out, register_1_q, shifter_3_out;
  wire [6:0] multiplexer_11_out, shifter_3_out_2;
  wire [7:0] multiplexer_1_out, multiplexer_2_out, multiplexer_3_out, multiplexer_9_out, multiplexer_13_out,
       n8_bit_cla_2_out_4, n8_bit_cla_3_out_4, n8_bit_cla_4_out_4, n8_bit_cla_5_out_4, n8_bit_cla_6_out_4,
       not_1_out, not_21_out, not_22_out, not_23_out, QUOTIENT_out, result_div, shifter_2_out,
       shifter_3_out_3;
  wire [14:0] register_2_q;
  wire [15:0] multiplexer_6_out, multiplexer_14_out, result_mult;
  wire [16:0] multiplexer_4_out, multiplexer_5_out, shifter_1_out;

  or _2x (_2x_out, add2M, sub2M);
  // Probe on multiplexer_4_out
  // Probe on shifter_1_out
  Multiplexer #(.width(8), .enable("false")) multiplexer_1 (
    .in0(Multiplicand), .in1(shifter_2_out), .out(multiplexer_1_out), .sel(_2x_out));
  assign not_1_out = ~multiplexer_1_out;  // NOT_Gate not_1, 8 bits wide
  or sub (sub_out, subM, sub2M);
  Multiplexer #(.width(8), .enable("false")) multiplexer_2 (
    .in0(multiplexer_1_out), .in1(not_1_out), .out(multiplexer_2_out), .sel(sub_out));
  Multiplexer #(.width(8), .enable("false")) multiplexer_3 (
    .in0(multiplexer_2_out), .in1({8{1'b0}}), .out(multiplexer_3_out), .sel(doNothing));
  _8_bit_CLA u_8_bit_cla_1 (
    .A(result_mult[15:8]), .B(multiplexer_3_out), .out_4(multiplexer_4_out[16:9]), .Cin0(Cin_out));  // open: ovf
  Shifter #(.width(17), .shift("ar")) shifter_1 (.in(multiplexer_4_out), .\dist (5'b00010), .out(shifter_1_out));
  not not_2 (not_2_out, FIRST);
  Shifter shifter_2 (.in(Multiplicand), .\dist (3'b001), .out(shifter_2_out));
  // Probe on multiplexer_3_out
  or Cin (Cin_out, subM, sub2M);
  Multiplexer #(.width(9), .enable("false")) multiplexer_4 (
    .in0({Multiplier, 1'b0}), .in1({result_mult[7:0], register_1_q[0]}), .out(multiplexer_4_out[8:0]),
    .sel(not_3_out));
  not not_3 (not_3_out, FIRST);
  Register #(.width(17)) register_1 (
    .D(multiplexer_5_out), .en(not_4_out), .Q({result_mult, register_1_q[0]}), .clk(Clock), .clr(ctrl_mult));
  Multiplexer #(.width(17), .enable("false")) multiplexer_5 (
    .in0(multiplexer_4_out), .in1(shifter_1_out), .out(multiplexer_5_out), .sel(not_2_out));
  not not_4 (not_4_out, RDY_mult);
  Decoder #(.select(3), .enable("false")) decoder_1 (
    .out0(decoder_1_out0), .out1(decoder_1_out1), .out2(decoder_1_out2), .out3(add2M), .out4(sub2M),
    .out5(decoder_1_out5), .out6(decoder_1_out6), .out7(decoder_1_out7),
    .sel({result_mult[1:0], register_1_q[0]}));
  or or_1 (addM, decoder_1_out1, decoder_1_out2);
  or or_2 (subM, decoder_1_out5, decoder_1_out6);
  or or_3 (doNothing, decoder_1_out0, decoder_1_out7);
  // Probe on {result_mult[1:0], register_1_q[0]}
  not not_5 (not_5_out, _4);
  not not_6 (not_6_out, _2);
  not not_7 (not_7_out, _1);
  not not_8 (not_8_out, _2);
  not not_9 (not_9_out, _8);
  not not_10 (not_10_out, _4);
  not not_11 (not_11_out, _2);
  not not_12 (not_12_out, _1);
  T_Flip_Flop t_ff_1 (.clk(Clock), .T(1'b1), .Q(_1), .reset(or_4_out), .en(1'b1));  // open: Qn, preset
  or or_4 (or_4_out, ctrl_mult, ctrl_div);
  or or_5 (or_5_out, ctrl_mult, ctrl_div);
  or or_6 (or_6_out, ctrl_mult, ctrl_div);
  and LASTD (RDY_div, _8, not_5_out, not_6_out, not_7_out);
  and LASTM (RDY_mult, _4, not_8_out, _1);
  and u_FIRST (FIRST, not_9_out, not_10_out, not_11_out, not_12_out);
  and and_1 (and_1_out, 1'b1, _1);
  Multiplexer #(.width(16), .enable("false")) multiplexer_6 (
    .in0(result_mult), .in1({{8{1'b0}}, result_div}), .out(multiplexer_6_out), .sel(d_ff_1_q));
  D_Flip_Flop d_ff_1 (.clk(or_5_out), .D(ctrl_div), .Q(d_ff_1_q), .en(or_6_out));  // open: Qn, preset, reset
  and and_2 (and_2_out, and_1_out, _2);
  T_Flip_Flop t_ff_2 (.clk(Clock), .T(and_1_out), .Q(_2), .reset(or_4_out), .en(1'b1));  // open: Qn, preset
  Multiplexer #(.width(16), .enable("false")) multiplexer_7 (
    .in0(multiplexer_6_out), .in1({16{1'b0}}), .out(data_result), .sel(div0));
  not not_13 (not_13_out, Multiplier[0]);
  not not_14 (not_14_out, Multiplier[1]);
  not not_15 (not_15_out, Multiplier[2]);
  not not_16 (not_16_out, Multiplier[3]);
  not not_17 (not_17_out, Multiplier[4]);
  not not_18 (not_18_out, Multiplier[5]);
  not not_19 (not_19_out, Multiplier[6]);
  not not_20 (not_20_out, Multiplier[7]);
  Multiplexer #(.enable("false")) multiplexer_8 (.in0(RDY_mult), .in1(RDY_div), .out(data_resultRDY), .sel(d_ff_1_q));
  and and_3 (div0, not_13_out, not_14_out, not_15_out, not_16_out, not_17_out, not_18_out, not_19_out, not_20_out);
  assign not_21_out = ~Multiplier;  // NOT_Gate not_21, 8 bits wide
  Multiplexer #(.width(8), .enable("false")) multiplexer_9 (
    .in0(Multiplier), .in1(n8_bit_cla_4_out_4), .out(multiplexer_9_out), .sel(Multiplier[7]));
  assign not_22_out = ~multiplexer_9_out;  // NOT_Gate not_22, 8 bits wide
  _8_bit_CLA u_8_bit_cla_2 (.A(shifter_3_out_3), .B(not_22_out), .out_4(n8_bit_cla_2_out_4), .Cin0(1'b1));  // open: ovf
  _8_bit_CLA u_8_bit_cla_3 (
    .A(shifter_3_out_3), .B(multiplexer_9_out), .out_4(n8_bit_cla_3_out_4), .Cin0(1'b0));  // open: ovf
  and and_4 (and_4_out, and_2_out, _4);
  T_Flip_Flop t_ff_3 (.clk(Clock), .T(and_2_out), .Q(_4), .reset(or_4_out), .en(1'b1));  // open: Qn, preset
  Multiplexer #(.enable("false")) multiplexer_10 (
    .in0(1'b0), .in1(div0), .out(ovf_div__mult_in_verilog), .sel(d_ff_1_q));
  _8_bit_CLA u_8_bit_cla_4 (.A(not_21_out), .B(8'h1), .out_4(n8_bit_cla_4_out_4), .Cin0(1'b0));  // open: ovf
  Multiplexer #(.width(8), .enable("false")) multiplexer_11 (
    .in0(n8_bit_cla_2_out_4), .in1(n8_bit_cla_3_out_4), .out({msb, multiplexer_11_out}), .sel(sub_add));
  T_Flip_Flop t_ff_4 (.clk(Clock), .T(and_4_out), .Q(_8), .reset(or_4_out), .en(1'b1));  // open: Qn, preset
  Multiplexer #(.enable("false")) multiplexer_12 (.in0(1'b1), .in1(1'b0), .out(multiplexer_12_out[0]), .sel(msb));
  Multiplexer #(.width(8), .enable("false")) multiplexer_13 (
    .in0(Multiplicand), .in1(n8_bit_cla_5_out_4), .out(multiplexer_13_out), .sel(Multiplicand[7]));
  assign not_23_out = ~Multiplicand;  // NOT_Gate not_23, 8 bits wide
  Multiplexer #(.width(16), .enable("false")) multiplexer_14 (
    .in0({{8{1'b0}}, multiplexer_13_out}),
    .in1({msb, multiplexer_11_out, shifter_3_out_2, multiplexer_12_out[0]}), .out(multiplexer_14_out),
    .sel(not_25_out));
  not not_24 (not_24_out, RDY_div);
  not not_25 (not_25_out, FIRST);
  _8_bit_CLA u_8_bit_cla_5 (.A(not_23_out), .B(8'h1), .out_4(n8_bit_cla_5_out_4), .Cin0(1'b0));  // open: ovf
  Register #(.width(16)) register_2 (
    .D(multiplexer_14_out), .en(not_24_out), .Q({sub_add, register_2_q}), .clk(Clock), .clr(ctrl_div));
  assign QUOTIENT_out = ~multiplexer_14_out[7:0];  // NOT_Gate QUOTIENT, 8 bits wide
  xor xor_1 (xor_1_out, Multiplier[7], Multiplicand[7]);
  _8_bit_CLA u_8_bit_cla_6 (.A(QUOTIENT_out), .B(8'h1), .out_4(n8_bit_cla_6_out_4), .Cin0(1'b0));  // open: ovf
  Multiplexer #(.width(8), .enable("false")) multiplexer_15 (
    .in0(multiplexer_14_out[7:0]), .in1(n8_bit_cla_6_out_4), .out(result_div), .sel(xor_1_out));
  Shifter #(.width(16)) shifter_3 (
    .in({sub_add, register_2_q}), .\dist (4'b0001), .out({shifter_3_out_3, shifter_3_out_2, shifter_3_out[0]}));

  // Other names for the same wires on the sheet: Divisor[7:0] = Multiplier; NegDivisor = Multiplier[7]; clk = Clock;
  //   Dividend[7:0] = Multiplicand; NegDividend = Multiplicand[7]
endmodule

module counter_6_bit (
  output _0,
  output _17,
  output _32
);

  wire _1, _2, _4, _8, _16, _32_t, and_1_out, and_2_out, and_3_out, and_4_out, and_5_out, clk, not_1_out,
       not_2_out, not_3_out, not_4_out, not_5_out, not_6_out, not_7_out, not_8_out, not_9_out, not_10_out,
       not_11_out, not_12_out, not_13_out, not_14_out, not_15_out;

  Clock clock_1 (.out(clk));
  T_Flip_Flop t_ff_1 (.clk(clk), .T(1'b1), .Q(_1));  // open: Qn, preset, reset, en
  and and_1 (and_1_out, 1'b1, _1);
  T_Flip_Flop t_ff_2 (.clk(clk), .T(and_1_out), .Q(_2));  // open: Qn, preset, reset, en
  and and_2 (and_2_out, and_1_out, _2);
  T_Flip_Flop t_ff_3 (.clk(clk), .T(and_2_out), .Q(_4));  // open: Qn, preset, reset, en
  and and_3 (and_3_out, and_2_out, _4);
  T_Flip_Flop t_ff_4 (.clk(clk), .T(and_3_out), .Q(_8));  // open: Qn, preset, reset, en
  and and_4 (and_4_out, and_3_out, _8);
  T_Flip_Flop t_ff_5 (.clk(clk), .T(and_4_out), .Q(_16));  // open: Qn, preset, reset, en
  and and_5 (and_5_out, and_4_out, _16);
  T_Flip_Flop t_ff_6 (.clk(clk), .T(and_5_out), .Q(_32_t));  // open: Qn, preset, reset, en
  not not_1 (not_1_out, _32_t);
  not not_2 (not_2_out, _16);
  not not_3 (not_3_out, _8);
  not not_4 (not_4_out, _4);
  not not_5 (not_5_out, _2);
  not not_6 (not_6_out, _1);
  not not_7 (not_7_out, _32_t);
  not not_8 (not_8_out, _8);
  not not_9 (not_9_out, _4);
  not not_10 (not_10_out, _2);
  not not_11 (not_11_out, _16);
  not not_12 (not_12_out, _8);
  not not_13 (not_13_out, _4);
  not not_14 (not_14_out, _2);
  not not_15 (not_15_out, _1);
  and and_6 (_0, not_1_out, not_2_out, not_3_out, not_4_out, not_5_out, not_6_out);
  and and_7 (_17, not_7_out, _16, not_8_out, not_9_out, not_10_out, _1);
  and and_8 (_32, _32_t, not_11_out, not_12_out, not_13_out, not_14_out, not_15_out);
endmodule

module full_processor (
  input  in_1,
  input  Global_Reset,
  input  [4:0] _31_27_OP,
  input  [4:0] _26_22_RD,
  input  [4:0] _21_17_RS,
  input  [4:0] _16_12_RT,
  input  [31:0] NoOp,
  input  [4:0] _11_7_SHAMT,
  input  [4:0] _6_2_ALUOP,
  input  [1:0] _1_0_ZERO
);

  wire Addi_DX, Addi_FD, ALU_ILT, ALU_INE, ALU_Ovf, and_1_out, and_2_out, and_3_out, and_5_out, and_6_out,
       and_7_out, and_8_out, and_9_out, and_10_out, and_11_out, and_12_out, and_13_out, and_14_out,
       and_15_out, and_16_out, and_17_out, and_18_out, and_19_out, and_20_out, and_21_out, and_22_out,
       and_23_out, and_28_out, and_29_out, and_30_out, and_31_out, and_32_out, and_35_out, and_38_out,
       and_39_out, and_42_out, BEX_DX, Bex_FD, BEX_MW_BYPASS, BEX_NE, BEX_SETX_BYPASS_MW, BEX_SETX_BYPASS_XM,
       BEX_XM_BYPASS, BLT_DX, BNE_DX, Branch_FD, comparator_1_eq, comparator_2_eq, comparator_3_eq,
       comparator_4_eq, comparator_5_eq, comparator_6_eq, comparator_7_eq, comparator_8_eq, comparator_9_eq,
       comparator_10_eq, comparator_11_eq, comparator_12_eq, comparator_13_eq, comparator_14_eq,
       comparator_15_eq, comparator_16_eq, comparator_17_eq, comparator_18_eq, comparator_19_eq,
       comparator_20_eq, comparator_21_eq, comparator_22_eq, comparator_23_gt, comparator_23_lt,
       comparator_24_eq, comparator_25_eq, comparator_26_eq, Div_DX, div_ongoing, Div_Ongoing_q, div_start,
       fall, isDiv, isMult, J_DX, JAL_DX, JAL_MW, JAL_XM, JR_DX, JR_FD, LW_DX, LW_MW, LW_R1_STALL,
       LW_SW_Bypass, LW_XM, ModifiesRD_MW, ModifiesRD_XM, Mult_DX, mult_ongoing, Mult_Ongoing_q, mult_start,
       multdiv_ovf, multdiv_rdy, multiplexer_38_out, MW_R1_Bypass, MW_R2_Bypass, MW_RD_IS_0, NOOP_DX,
       NoOp_DX_t, NOOP_t, not_1_out, not_3_out, not_4_out, not_5_out, not_6_out, not_7_out, not_8_out,
       not_9_out, not_10_out, not_11_out, not_12_out, or_3_out, or_4_out, or_5_out, or_6_out, or_7_out,
       or_8_out, or_16_out, or_17_out, or_18_out, or_19_out, or_20_out, or_28_out, or_29_out, or_30_out,
       or_31_out, or_32_out, rise, RType_DX, Rtype_FD, SETX_DX, SetX_MW, SETX_MW_R1_Bypass,
       SETX_MW_R2_Bypass, SetX_XM, SETX_XM_R1_Bypass, SETX_XM_R2_Bypass, Stall_DX, Stall_FD, Stall_PC,
       SW_BYPASS_MW, SW_BYPASS_XM, SW_DX, SW_XM, WEn_mw, XM_R1_Bypass, XM_R2_Bypass, XM_RD_IS_0;
  wire [4:0] ALU_Op_MW, ALUOp, ALUOp_XM, final_reg_dest, multiplexer_3_out, multiplexer_4_out,
       multiplexer_5_out, multiplexer_6_out, multiplexer_7_out, multiplexer_27_out, multiplexer_28_out,
       OpCode_MW, Opcode_XM, RD_DX, RD_FD, RD_XM, RS_DX, RS_FD, RT_DX, RT_FD, Shamt;
  wire [16:0] Immediate_17;
  wire [26:0] Target_DX;
  wire [31:0] ALU_XM, ALUOut, data_out_mw, data_to_write, Immediate_32, Instr_DX, Instr_FD, Instr_XM,
       multdiv_result, multiplexer_1_out, multiplexer_2_out, multiplexer_8_out, multiplexer_9_out,
       multiplexer_10_out, multiplexer_11_out, multiplexer_12_out, multiplexer_13_out, multiplexer_14_out,
       multiplexer_15_out, multiplexer_16_out, multiplexer_17_out, multiplexer_18_out, multiplexer_19_out,
       multiplexer_20_out, multiplexer_21_out, multiplexer_22_out, multiplexer_23_out, multiplexer_24_out,
       multiplexer_25_out, multiplexer_26_out, multiplexer_29_out, multiplexer_30_out, multiplexer_31_out,
       multiplexer_32_out, multiplexer_33_out, multiplexer_34_out, multiplexer_35_out, multiplexer_40_out,
       multiplexer_41_out, n32_bit_carry_lookahead_3_s, PC, PC_1, PC_DX, PC_DX_1, PC_FD, PC_MW, PC_MW_1,
       PC_XM, ram_1_data, Read1_DX, Read1_XM, Read2_DX, ReadA, ReadB, real_alu_in1, real_alu_in2,
       Real_Read1_DX, Target_DX_Extended, Target_MW, Target_XM_Extended;

  Clock Global_Clk (.out(rise));
  Register #(.width(32)) PC_REG (.D(multiplexer_24_out), .en(not_1_out), .Q(PC), .clk(rise), .clr(Global_Reset));
  not not_1 (not_1_out, Stall_PC);
  // Probe on PC
  not not_2 (fall, rise);
  and and_1 (and_1_out, BLT_DX, ALU_ILT);
  and and_2 (and_2_out, BEX_NE, BEX_DX);
  and and_3 (and_3_out, BNE_DX, ALU_INE);
  ROM #(.addrWidth(12), .dataWidth(32)) rom_1 (.addr(PC[11:0]), .sel(fall));  // open: data
  Multiplexer #(.width(32), .enable("false")) multiplexer_1 (
    .in0({_31_27_OP, _26_22_RD, _21_17_RS, _16_12_RT, _11_7_SHAMT, _6_2_ALUOP, _1_0_ZERO}), .in1(NoOp),
    .out(multiplexer_1_out), .sel(in_1));
  _32_bit_carry_lookahead u_32_bit_carry_lookahead_1 (.A_32(PC), .B_32(32'h1), .C0(1'b0), .S(PC_1));  // open: Overflow
  or or_1 (NOOP_DX, LW_R1_STALL, and_3_out, J_DX, and_1_out, JR_DX, JAL_DX, and_2_out);
  or or_2 (NOOP_t, J_DX, and_3_out, and_1_out, JR_DX, JAL_DX, and_2_out);
  // Probe on {_31_27_OP, _26_22_RD, _21_17_RS, _16_12_RT, _11_7_SHAMT, _6_2_ALUOP, _1_0_ZERO}
  Multiplexer #(.width(32), .enable("false")) multiplexer_2 (
    .in0(multiplexer_1_out), .in1({32{1'b0}}), .out(multiplexer_2_out), .sel(NOOP_t));
  FD_Module fd_module_1 (
    .Instruction(multiplexer_2_out), .Stall(Stall_FD), .Clock(rise), .Reset(Global_Reset),
    .Instruction_FD(Instr_FD), .Rt(RT_FD), .Rs(RS_FD), .Rd(RD_FD), .PC(PC), .PC_OUT(PC_FD),
    .R_Type(Rtype_FD), .Bex(Bex_FD), .Addi(Addi_FD), .Branch(Branch_FD), .JR(JR_FD));
  or or_3 (or_3_out, RType_DX, SW_DX, Addi_DX, LW_DX);
  Multiplexer #(.width(5), .enable("false")) multiplexer_3 (
    .in0(RD_FD), .in1(5'b11110), .out(multiplexer_3_out), .sel(Bex_FD));
  or or_4 (or_4_out, div_ongoing, mult_ongoing);
  not not_3 (not_3_out, multdiv_rdy);
  or or_5 (or_5_out, Rtype_FD, Branch_FD, Addi_FD);
  Comparator #(.width(5)) comparator_1 (.a(RS_DX), .b(5'b11110), .eq(comparator_1_eq));  // open: gt, lt
  Comparator #(.width(5)) comparator_2 (.a(RS_DX), .b(5'b11110), .eq(comparator_2_eq));  // open: gt, lt
  Comparator #(.width(5)) comparator_3 (.a(RT_DX), .b(5'b11110), .eq(comparator_3_eq));  // open: gt, lt
  Comparator #(.width(5)) comparator_4 (.a(RT_DX), .b(5'b11110), .eq(comparator_4_eq));  // open: gt, lt
  Comparator #(.width(5)) comparator_5 (.a(RD_DX), .b(5'b11110), .eq(comparator_5_eq));  // open: gt, lt
  or or_6 (or_6_out, BNE_DX, JR_DX, BLT_DX);
  Comparator #(.width(5)) comparator_6 (.a(RD_DX), .b(5'b11110), .eq(comparator_6_eq));  // open: gt, lt
  Comparator #(.width(5)) comparator_7 (.a(RS_DX), .b(5'b11110), .eq(comparator_7_eq));  // open: gt, lt
  or or_7 (or_7_out, BNE_DX, BLT_DX);
  Comparator #(.width(5)) comparator_8 (.a(RS_DX), .b(5'b11110), .eq(comparator_8_eq));  // open: gt, lt
  Multiplexer #(.width(5), .enable("false")) multiplexer_4 (
    .in0(multiplexer_3_out), .in1(RS_FD), .out(multiplexer_4_out), .sel(Rtype_FD));
  Multiplexer #(.width(5), .enable("false")) multiplexer_5 (
    .in0(RS_FD), .in1(RT_FD), .out(multiplexer_5_out), .sel(Rtype_FD));
  and and_4 (Stall_DX, or_4_out, not_3_out);
  Comparator #(.width(5)) comparator_9 (.a(RD_DX), .b(RS_FD), .eq(comparator_9_eq));  // open: gt, lt
  Comparator #(.width(5)) comparator_10 (.a(RD_DX), .b(RT_FD), .eq(comparator_10_eq));  // open: gt, lt
  or or_8 (or_8_out, Branch_FD, JR_FD);
  Comparator #(.width(5)) comparator_11 (.a(RD_DX), .b(RD_FD), .eq(comparator_11_eq));  // open: gt, lt
  Comparator #(.width(5)) comparator_12 (.a(RD_DX), .b(5'b11110), .eq(comparator_12_eq));  // open: gt, lt
  Multiplexer #(.width(5), .enable("false")) multiplexer_6 (
    .in0(multiplexer_7_out), .in1(5'b11110), .out(multiplexer_6_out), .sel(SetX_MW));
  or or_9 (Stall_PC, LW_R1_STALL, Stall_DX);
  or or_10 (Stall_FD, LW_R1_STALL, Stall_DX);
  and and_5 (and_5_out, comparator_1_eq, or_3_out, SetX_XM);
  and and_6 (and_6_out, comparator_2_eq, or_3_out, SetX_MW);
  and and_7 (and_7_out, RType_DX, comparator_3_eq, SetX_XM);
  and and_8 (and_8_out, RType_DX, comparator_4_eq, SetX_MW);
  and and_9 (and_9_out, comparator_5_eq, SetX_XM, or_6_out);
  and and_10 (and_10_out, or_6_out, SetX_MW, comparator_6_eq);
  and and_11 (and_11_out, comparator_7_eq, SetX_XM, or_7_out);
  and and_12 (and_12_out, or_7_out, SetX_MW, comparator_8_eq);
  Multiplexer #(.width(5), .enable("false")) multiplexer_7 (
    .in0(final_reg_dest), .in1({5{1'b1}}), .out(multiplexer_7_out), .sel(JAL_MW));
  Multiplexer #(.width(32), .enable("false")) multiplexer_8 (
    .in0(multiplexer_9_out), .in1(Target_MW), .out(multiplexer_8_out), .sel(SetX_MW));
  and and_13 (and_13_out, or_5_out, comparator_9_eq, LW_DX);
  and and_14 (and_14_out, Rtype_FD, comparator_10_eq, LW_DX);
  and and_15 (and_15_out, or_8_out, comparator_11_eq, LW_DX);
  and and_16 (and_16_out, Bex_FD, comparator_12_eq, LW_DX);
  Multiplexer #(.width(32), .enable("false")) multiplexer_9 (
    .in0(data_out_mw), .in1(PC_MW_1), .out(multiplexer_9_out), .sel(JAL_MW));
  register_files register_files_1 (
    .data_writeReg(multiplexer_8_out), .clk(fall), .ctrl_reset(Global_Reset), .ctrl_writeEnable(WEn_mw),
    .ctrl_writeReg(multiplexer_6_out), .ctrl_readRegA(multiplexer_4_out), .ctrl_readRegB(multiplexer_5_out),
    .data_readRegA(ReadA), .data_readRegB(ReadB));
  or or_11 (LW_R1_STALL, and_13_out, and_14_out, and_15_out, and_16_out);
  or or_12 (SETX_XM_R1_Bypass, and_5_out, and_9_out);
  or or_13 (SETX_MW_R1_Bypass, and_6_out, and_10_out);
  or or_14 (SETX_XM_R2_Bypass, and_7_out, and_11_out);
  or or_15 (SETX_MW_R2_Bypass, and_8_out, and_12_out);
  Multiplexer #(.width(32), .enable("false")) multiplexer_10 (
    .in0(Read1_DX), .in1(data_out_mw), .out(multiplexer_10_out), .sel(BEX_MW_BYPASS));
  _32_bit_carry_lookahead u_32_bit_carry_lookahead_2 (
    .A_32(PC_DX), .B_32(32'h1), .C0(1'b0), .S(PC_DX_1));  // open: Overflow
  Multiplexer #(.width(32), .enable("false")) multiplexer_11 (
    .in0(Instr_FD), .in1({32{1'b0}}), .out(multiplexer_11_out), .sel(NOOP_DX));
  Multiplexer #(.width(32), .enable("false")) multiplexer_12 (
    .in0(ReadA), .in1({32{1'b0}}), .out(multiplexer_12_out), .sel(NOOP_DX));
  Multiplexer #(.width(32), .enable("false")) multiplexer_13 (
    .in0(ReadB), .in1({32{1'b0}}), .out(multiplexer_13_out), .sel(NOOP_DX));
  or or_16 (or_16_out, J_DX, JAL_DX, and_17_out);
  DX_Module dx_module_1 (
    .Stall(Stall_DX), .PC(PC_FD), .Clock(rise), .Reset(Global_Reset), .Instruction(multiplexer_11_out),
    .Read1_In(multiplexer_12_out), .Read2_In(multiplexer_13_out), .PC_OUT(PC_DX), .Instruction_Out(Instr_DX),
    .ALUop(ALUOp), .Shamt(Shamt), .Immediate(Immediate_17), .Read1_Out(Read1_DX), .Read2_Out(Read2_DX),
    .R_Type(RType_DX), .Addi(Addi_DX), .Sw(SW_DX), .Lw(LW_DX), .J(J_DX), .Bne(BNE_DX), .Jal(JAL_DX),
    .Blt(BLT_DX), .Bex(BEX_DX), .SetX(SETX_DX), .Mult(Mult_DX), .Div(Div_DX), .Target(Target_DX), .RS(RS_DX),
    .RT(RT_DX), .ZeroInstruction(NoOp_DX_t), .RD(RD_DX), .Jr(JR_DX));
  Multiplexer #(.width(32), .enable("false")) multiplexer_14 (
    .in0(multiplexer_10_out), .in1(data_to_write), .out(multiplexer_14_out), .sel(BEX_XM_BYPASS));
  Multiplexer #(.width(32), .enable("false")) multiplexer_15 (
    .in0(PC_1), .in1(Target_DX_Extended), .out(multiplexer_15_out), .sel(or_16_out));
  and and_17 (and_17_out, BEX_NE, BEX_DX);
  _32_bit_carry_lookahead u_32_bit_carry_lookahead_3 (
    .A_32(PC_DX_1), .B_32(Immediate_32), .C0(1'b0), .S(n32_bit_carry_lookahead_3_s));  // open: Overflow
  Multiplexer #(.width(32), .enable("false")) multiplexer_16 (
    .in0(multiplexer_14_out), .in1(Target_MW), .out(multiplexer_16_out), .sel(BEX_SETX_BYPASS_MW));
  or or_17 (or_17_out, BNE_DX, BLT_DX);
  Multiplexer #(.width(32), .enable("false")) multiplexer_17 (
    .in0(multiplexer_15_out), .in1(n32_bit_carry_lookahead_3_s), .out(multiplexer_17_out), .sel(or_18_out));
  or or_18 (or_18_out, and_19_out, and_18_out);
  and and_18 (and_18_out, ALU_ILT, BLT_DX);
  and and_19 (and_19_out, BNE_DX, ALU_INE);
  Comparator #(.width(5)) comparator_13 (.a(RS_DX), .b(RD_XM), .eq(comparator_13_eq));  // open: gt, lt
  or or_19 (or_19_out, RType_DX, SW_DX, LW_DX, Addi_DX);
  not not_4 (not_4_out, XM_RD_IS_0);
  Comparator #(.width(5)) comparator_14 (.a(RS_DX), .b(final_reg_dest), .eq(comparator_14_eq));  // open: gt, lt
  not not_5 (not_5_out, MW_RD_IS_0);
  Comparator #(.width(5)) comparator_15 (.a(RT_DX), .b(RD_XM), .eq(comparator_15_eq));  // open: gt, lt
  not not_6 (not_6_out, XM_RD_IS_0);
  not not_7 (not_7_out, Addi_DX);
  Comparator #(.width(5)) comparator_16 (.a(RT_DX), .b(final_reg_dest), .eq(comparator_16_eq));  // open: gt, lt
  not not_8 (not_8_out, MW_RD_IS_0);
  not not_9 (not_9_out, Addi_DX);
  Comparator #(.width(5)) comparator_17 (.a(RD_DX), .b(RD_XM), .eq(comparator_17_eq));  // open: gt, lt
  or or_20 (or_20_out, BNE_DX, JR_DX, BLT_DX);
  Comparator #(.width(5)) comparator_18 (.a(RD_DX), .b(final_reg_dest), .eq(comparator_18_eq));  // open: gt, lt
  Comparator #(.width(5)) comparator_19 (.a(RS_DX), .b(RD_XM), .eq(comparator_19_eq));  // open: gt, lt
  Comparator #(.width(5)) comparator_20 (.a(RS_DX), .b(final_reg_dest), .eq(comparator_20_eq));  // open: gt, lt
  Comparator #(.width(5)) comparator_21 (.a(RD_XM), .b(5'b11110), .eq(comparator_21_eq));  // open: gt, lt
  Comparator #(.width(5)) comparator_22 (.a(final_reg_dest), .b(5'b11110), .eq(comparator_22_eq));  // open: gt, lt
  Multiplexer #(.width(32), .enable("false")) multiplexer_18 (
    .in0(multiplexer_16_out), .in1(Target_XM_Extended), .out(multiplexer_18_out), .sel(BEX_SETX_BYPASS_XM));
  and and_20 (and_20_out, comparator_17_eq, ModifiesRD_XM, or_20_out);
  and and_21 (and_21_out, or_20_out, ModifiesRD_MW, comparator_18_eq);
  and and_22 (and_22_out, comparator_19_eq, ModifiesRD_XM, or_17_out);
  and and_23 (and_23_out, or_17_out, ModifiesRD_MW, comparator_20_eq);
  and and_24 (BEX_XM_BYPASS, comparator_21_eq, ModifiesRD_XM, BEX_DX);
  and and_25 (BEX_MW_BYPASS, BEX_DX, ModifiesRD_MW, comparator_22_eq);
  and and_26 (BEX_SETX_BYPASS_XM, SetX_XM, BEX_DX);
  and and_27 (BEX_SETX_BYPASS_MW, SetX_MW, BEX_DX);
  Multiplexer #(.width(32), .enable("false")) multiplexer_19 (
    .in0(multiplexer_17_out), .in1(Read1_DX), .out(multiplexer_19_out), .sel(JR_DX));
  Comparator #(.width(32)) comparator_23 (
    .a(multiplexer_18_out), .b({32{1'b0}}), .gt(comparator_23_gt), .lt(comparator_23_lt));  // open: eq
  and and_28 (and_28_out, comparator_13_eq, NoOp_DX_t, ModifiesRD_XM, or_19_out, not_4_out);
  and and_29 (and_29_out, or_19_out, NoOp_DX_t, ModifiesRD_MW, comparator_14_eq, not_5_out);
  and and_30 (and_30_out, comparator_15_eq, NoOp_DX_t, not_7_out, RType_DX, not_6_out, ModifiesRD_XM);
  and and_31 (and_31_out, RType_DX, NoOp_DX_t, not_9_out, comparator_16_eq, not_8_out, ModifiesRD_MW);
  and and_32 (and_32_out, JR_DX, MW_R1_Bypass);
  and and_33 (isMult, Mult_DX, RType_DX);
  and and_34 (isDiv, Div_DX, RType_DX);
  or or_21 (BEX_NE, comparator_23_gt, comparator_23_lt);
  or or_22 (XM_R1_Bypass, and_28_out, and_20_out);
  or or_23 (MW_R1_Bypass, and_29_out, and_21_out);
  or or_24 (XM_R2_Bypass, and_30_out, and_22_out);
  or or_25 (MW_R2_Bypass, and_31_out, and_23_out);
  Multiplexer #(.width(32), .enable("false")) multiplexer_20 (
    .in0(multiplexer_19_out), .in1(data_out_mw), .out(multiplexer_20_out), .sel(and_32_out));
  D_Flip_Flop u_Mult_Ongoing (.clk(rise), .D(isMult), .Q(Mult_Ongoing_q));  // open: Qn, preset, en, reset
  D_Flip_Flop u_Div_Ongoing (.clk(rise), .D(isDiv), .Q(Div_Ongoing_q));  // open: Qn, preset, en, reset
  Multiplexer #(.width(32), .enable("false")) multiplexer_21 (
    .in0(multiplexer_20_out), .in1(data_to_write), .out(multiplexer_21_out), .sel(and_35_out));
  and and_35 (and_35_out, JR_DX, XM_R1_Bypass);
  not not_10 (not_10_out, Mult_Ongoing_q);
  not not_11 (not_11_out, Div_Ongoing_q);
  not not_12 (not_12_out, multdiv_rdy);
  and and_36 (mult_start, not_10_out, not_12_out, isMult);
  and and_37 (div_start, not_11_out, not_12_out, isDiv);
  Multiplexer #(.width(32), .enable("false")) multiplexer_22 (
    .in0(multiplexer_21_out), .in1(Target_MW), .out(multiplexer_22_out), .sel(and_38_out));
  and and_38 (and_38_out, JR_DX, SETX_MW_R1_Bypass);
  or or_26 (mult_ongoing, Mult_Ongoing_q, mult_start);
  or or_27 (div_ongoing, Div_Ongoing_q, div_start);
  Multiplexer #(.width(32), .enable("false")) multiplexer_23 (
    .in0(Read2_DX), .in1(Read1_DX), .out(multiplexer_23_out), .sel(or_28_out));
  or or_28 (or_28_out, BNE_DX, BLT_DX);
  Comparator #(.width(5)) comparator_24 (.a(RD_DX), .b(RD_XM), .eq(comparator_24_eq));  // open: gt, lt
  Comparator #(.width(5)) comparator_25 (.a(RD_DX), .b(final_reg_dest), .eq(comparator_25_eq));  // open: gt, lt
  or or_29 (or_29_out, Addi_DX, SW_DX, LW_DX);
  Multiplexer #(.width(32), .enable("false")) multiplexer_24 (
    .in0(multiplexer_22_out), .in1(Target_XM_Extended), .out(multiplexer_24_out), .sel(and_39_out));
  and and_39 (and_39_out, JR_DX, SETX_XM_R1_Bypass);
  or or_30 (or_30_out, BLT_DX, BNE_DX);
  Multiplexer #(.width(32), .enable("false")) multiplexer_25 (
    .in0(multiplexer_23_out), .in1(Read1_DX), .out(multiplexer_25_out), .sel(RType_DX));
  Multiplexer #(.width(32), .enable("false")) multiplexer_26 (
    .in0(Read2_DX), .in1(Immediate_32), .out(multiplexer_26_out), .sel(or_29_out));
  and and_40 (SW_BYPASS_XM, comparator_24_eq, SW_DX, ModifiesRD_XM);
  and and_41 (SW_BYPASS_MW, comparator_25_eq, SW_DX, ModifiesRD_MW);
  Multiplexer #(.width(5), .enable("false")) multiplexer_27 (
    .in0(ALUOp), .in1(5'b00001), .out(multiplexer_27_out), .sel(or_30_out));
  multdiv multdiv_1 (
    .ctrl_mult(mult_start), .ctrl_div(div_start), .clock(rise), .DataA(real_alu_in1), .DataB(real_alu_in2),
    .data_result(multdiv_result), .data_exception(multdiv_ovf), .data_resultRDY(multdiv_rdy));
  Multiplexer #(.width(5), .enable("false")) multiplexer_28 (
    .in0(multiplexer_27_out), .in1({5{1'b0}}), .out(multiplexer_28_out), .sel(or_31_out));
  or or_31 (or_31_out, Addi_DX, LW_DX, SW_DX);
  Multiplexer #(.width(32), .enable("false")) multiplexer_29 (
    .in0(multiplexer_25_out), .in1(data_out_mw), .out(multiplexer_29_out), .sel(MW_R1_Bypass));
  Multiplexer #(.width(32), .enable("false")) multiplexer_30 (
    .in0(multiplexer_26_out), .in1(data_out_mw), .out(multiplexer_30_out), .sel(MW_R2_Bypass));
  main_alu main_alu_1 (
    .InputA(real_alu_in1), .InputB(real_alu_in2), .shift_amt(Shamt), .opcode(multiplexer_28_out),
    .out_5(ALUOut), .overflow(ALU_Ovf), .isNotEqual(ALU_INE), .isLessThan(ALU_ILT));
  Multiplexer #(.width(32), .enable("false")) multiplexer_31 (
    .in0(multiplexer_29_out), .in1(data_to_write), .out(multiplexer_31_out), .sel(XM_R1_Bypass));
  Multiplexer #(.width(32), .enable("false")) multiplexer_32 (
    .in0(multiplexer_30_out), .in1(data_to_write), .out(multiplexer_32_out), .sel(XM_R2_Bypass));
  or or_32 (or_32_out, isMult, isDiv);
  Multiplexer #(.width(32), .enable("false")) multiplexer_33 (
    .in0(multiplexer_32_out), .in1(Target_MW), .out(multiplexer_33_out), .sel(SETX_MW_R2_Bypass));
  Multiplexer #(.width(32), .enable("false")) multiplexer_34 (
    .in0(Read1_DX), .in1(data_out_mw), .out(multiplexer_34_out), .sel(SW_BYPASS_MW));
  and and_42 (and_42_out, or_32_out, multdiv_rdy);
  assign Immediate_32 = {{15{1'b0}}, Immediate_17};  // Bit_Extender bit_extender_1
  assign Target_DX_Extended = {{5{1'b0}}, Target_DX};  // Bit_Extender bit_extender_2
  Multiplexer #(.width(32), .enable("false")) multiplexer_35 (
    .in0(multiplexer_31_out), .in1(Target_MW), .out(multiplexer_35_out), .sel(SETX_MW_R1_Bypass));
  Multiplexer #(.width(32), .enable("false")) multiplexer_36 (
    .in0(multiplexer_33_out), .in1(Target_XM_Extended), .out(real_alu_in2), .sel(SETX_XM_R2_Bypass));
  Multiplexer #(.width(32), .enable("false")) multiplexer_37 (
    .in0(multiplexer_34_out), .in1(ALU_XM), .out(Real_Read1_DX), .sel(SW_BYPASS_XM));
  Multiplexer #(.enable("false")) multiplexer_38 (
    .in0(1'b0), .in1(multdiv_ovf), .out(multiplexer_38_out), .sel(and_42_out));
  Multiplexer #(.width(32), .enable("false")) multiplexer_39 (
    .in0(multiplexer_35_out), .in1(Target_XM_Extended), .out(real_alu_in1), .sel(SETX_XM_R1_Bypass));
  Multiplexer #(.width(32), .enable("false")) multiplexer_40 (
    .in0(ALUOut), .in1(multdiv_result), .out(multiplexer_40_out), .sel(and_42_out));
  XM_Module xm_module_1 (
    .PC(PC_DX), .ALU_Output(multiplexer_40_out), .Instruction(Instr_DX), .Stall(Stall_DX), .Clock(rise),
    .Reset(Global_Reset), .PC_OUT(PC_XM), .ALU_Out_XM(ALU_XM), .Instruction_Out(Instr_XM), .Sw(SW_XM),
    .Lw(LW_XM), .ovf(ALU_Ovf), .Read1_DX(Real_Read1_DX), .Read1_XM(Read1_XM), .Target_In(Target_DX_Extended),
    .Target_Out(Target_XM_Extended), .RD_XM(RD_XM), .Opcode(Opcode_XM), .RD_Is_Zero_Register(XM_RD_IS_0),
    .SetX(SetX_XM), .ALUOP(ALUOp_XM), .JAL(JAL_XM), .ModifiesRD(ModifiesRD_XM), .ALUOpDX(ALUOp),
    .MultOvf(multiplexer_38_out));
  Multiplexer #(.width(32), .enable("false")) multiplexer_41 (
    .in0(Read1_XM), .in1(data_out_mw), .out(multiplexer_41_out), .sel(LW_SW_Bypass));
  Comparator #(.width(5)) comparator_26 (.a(RD_XM), .b(final_reg_dest), .eq(comparator_26_eq));  // open: gt, lt
  and and_43 (LW_SW_Bypass, comparator_26_eq, LW_MW, SW_XM);
  RAM #(.addrWidth(12), .dataWidth(32), .bus("separate")) ram_1 (
    .addr(ALU_XM[11:0]), .din(multiplexer_41_out), .data(ram_1_data), .str(SW_XM), .clk(rise), .ld(LW_XM));  // open: sel, clr
  Multiplexer #(.width(32), .enable("false")) multiplexer_42 (
    .in0(ALU_XM), .in1(ram_1_data), .out(data_to_write), .sel(LW_XM));
  _32_bit_carry_lookahead u_32_bit_carry_lookahead_4 (
    .A_32(PC_MW), .B_32(32'h1), .C0(1'b0), .S(PC_MW_1));  // open: Overflow
  MW_Module mw_module_1 (
    .PC(PC_XM), .Stall(Stall_DX), .Clock(rise), .Reset(Global_Reset), .Instruction(Instr_XM),
    .Data_In(data_to_write), .PC_OUT(PC_MW), .Data_to_write(data_out_mw), .Destination_Reg(final_reg_dest),
    .WEnable(WEn_mw), .Target_In(Target_XM_Extended), .Target_Out(Target_MW), .SetX_MW(SetX_MW),
    .ALUOp(ALU_Op_MW), .LW_MW(LW_MW), .RD_Is_Zero_Register(MW_RD_IS_0), .OpCode(OpCode_MW), .JAL_MW(JAL_MW),
    .ModifiesRD_MW(ModifiesRD_MW));

  // Other names for the same wires on the sheet: final_data_out[31:0] = data_out_mw; RD_MW[4:0] = final_reg_dest;
  //   reset = Global_Reset; Stall_MW = Stall_DX; Stall_XM = Stall_DX;
  //   Test[31:0] = {_31_27_OP, _26_22_RD, _21_17_RS, _16_12_RT, _11_7_SHAMT, _6_2_ALUOP, _1_0_ZERO}

  // Notes on the sheet:
  //   contents of rom_1 (hex, n*v repeats v):
  //   28440008 40820000 38540000 40d40000 1023000
  //   NOOPs
  //   ByPass for SetX followed by instructions that want to use it
  //   Stall Logic for Mult/Div and JAL
  //   NO-OP for LW Followed Immediately by Rtype/Addi/Branch/JR that Uses Same Destination Reg
  //   PC+1 Calculations for BNE and BLT
  //   ByPass for R Type, LW, SW, BNE, BLT, JRand Addi Instructions
  //   Bex ByPass for getting new RStatus
  //   Bypass for JR but JAL hasn't written
  //   ByPass for SW following an instruction that hasn't written yet
  //   Inputs to send to ALU
  //   LW Followed by SW Bypass
  //   Jal PC Calculation
endmodule

module FD_Module (
  input  [31:0] PC,
  input  [31:0] Instruction,
  input  Stall,
  input  Clock,
  input  Reset,
  output [31:0] PC_OUT,
  output [31:0] Instruction_FD,
  output [4:0] Rt,
  output [4:0] Rs,
  output [4:0] Rd,
  output R_Type,
  output Bex,
  output Addi,
  output Branch,
  output JR
);

  wire BLT_out, BNE_out, not_1_out, not_2_out, not_3_out, not_4_out, not_5_out, not_6_out, not_7_out,
       not_8_out, not_9_out, not_10_out, not_11_out, not_12_out, not_13_out, not_14_out, not_15_out,
       not_16_out, not_17_out, not_18_out, not_19_out, not_20_out, not_21_out, not_22_out, not_23_out;

  not not_1 (not_1_out, Stall);
  not not_2 (not_2_out, Stall);
  Register #(.width(32)) register_1 (.D(Instruction), .en(not_1_out), .Q(Instruction_FD), .clk(Clock), .clr(Reset));
  Register #(.width(32)) register_2 (.D(PC), .en(not_2_out), .Q(PC_OUT), .clk(Clock), .clr(Reset));
  not not_3 (not_3_out, Instruction_FD[29]);
  not not_4 (not_4_out, Instruction_FD[31]);
  not not_5 (not_5_out, Instruction_FD[27]);
  not not_6 (not_6_out, Instruction_FD[28]);
  not not_7 (not_7_out, Instruction_FD[30]);
  and u_R_Type (R_Type, not_4_out, not_7_out, not_3_out, not_6_out, not_5_out);
  not not_8 (not_8_out, Instruction_FD[31]);
  not not_9 (not_9_out, Instruction_FD[30]);
  not not_10 (not_10_out, Instruction_FD[27]);
  not not_11 (not_11_out, Instruction_FD[30]);
  and u_Bex (Bex, Instruction_FD[31], not_11_out, Instruction_FD[29], Instruction_FD[28], not_10_out);
  and u_Addi (Addi, not_8_out, not_9_out, Instruction_FD[29], not_13_out, Instruction_FD[27]);
  not not_12 (not_12_out, Instruction_FD[27]);
  not not_13 (not_13_out, Instruction_FD[28]);
  not not_14 (not_14_out, Instruction_FD[29]);
  not not_15 (not_15_out, Instruction_FD[31]);
  not not_16 (not_16_out, Instruction_FD[30]);
  and BNE (BNE_out, not_15_out, not_16_out, not_14_out, Instruction_FD[28], not_12_out);
  not not_17 (not_17_out, Instruction_FD[30]);
  not not_18 (not_18_out, Instruction_FD[31]);
  not not_19 (not_19_out, Instruction_FD[31]);
  not not_20 (not_20_out, Instruction_FD[27]);
  and BLT (BLT_out, not_18_out, not_17_out, Instruction_FD[29], Instruction_FD[28], not_20_out);
  or or_1 (Branch, BNE_out, BLT_out);
  not not_21 (not_21_out, Instruction_FD[27]);
  not not_22 (not_22_out, Instruction_FD[30]);
  not not_23 (not_23_out, Instruction_FD[28]);
  and u_JR (JR, not_19_out, not_22_out, Instruction_FD[29], not_23_out, not_21_out);

  assign Rd = Instruction_FD[26:22];
  assign Rs = Instruction_FD[21:17];
  assign Rt = Instruction_FD[16:12];

  // Other names for the same wires on the sheet: Opcode[4:0] = Instruction_FD[31:27]
endmodule

module DX_Module (
  input  Stall,
  input  [31:0] PC,
  input  Clock,
  input  Reset,
  input  [31:0] Instruction,
  input  [31:0] Read1_In,
  input  [31:0] Read2_In,
  output [31:0] PC_OUT,
  output [31:0] Instruction_Out,
  output [4:0] ALUop,
  output [4:0] Shamt,
  output [4:0] RT,
  output [16:0] Immediate,
  output [4:0] RS,
  output [26:0] Target,
  output [4:0] RD,
  output [31:0] Read1_Out,
  output ZeroInstruction,
  output [31:0] Read2_Out,
  output R_Type,
  output Addi,
  output Sw,
  output Lw,
  output J,
  output Bne,
  output Jal,
  output Jr,
  output Blt,
  output Bex,
  output SetX,
  output Mult,
  output Div
);

  wire not_1_out, not_2_out, not_3_out, not_4_out, not_5_out, not_6_out, not_7_out, not_8_out, not_9_out,
       not_10_out, not_11_out, not_12_out, not_13_out, not_14_out, not_15_out, not_16_out, not_17_out,
       not_18_out, not_19_out, not_20_out, not_21_out, not_22_out, not_23_out, not_24_out, not_25_out,
       not_26_out, not_27_out, not_28_out, not_29_out, not_30_out, not_31_out, not_32_out, not_33_out,
       not_34_out, not_35_out, not_36_out, not_37_out, not_38_out, not_39_out, not_40_out, not_41_out,
       not_42_out, not_43_out, not_44_out, not_45_out;

  not not_1 (not_1_out, Instruction_Out[30]);
  not not_2 (not_2_out, Instruction_Out[31]);
  not not_3 (not_3_out, Stall);
  not not_4 (not_4_out, Instruction_Out[28]);
  not not_5 (not_5_out, Instruction_Out[30]);
  not not_6 (not_6_out, Instruction_Out[27]);
  not not_7 (not_7_out, Instruction_Out[28]);
  not not_8 (not_8_out, Instruction_Out[31]);
  not not_9 (not_9_out, Instruction_Out[29]);
  and u_R_Type (R_Type, not_2_out, not_1_out, not_9_out, not_4_out, not_6_out);
  and u_Addi (Addi, not_8_out, not_5_out, Instruction_Out[29], not_7_out, Instruction_Out[27]);
  not not_10 (not_10_out, Stall);
  Register #(.width(32)) register_1 (
    .D(Instruction), .en(not_3_out), .Q({Instruction_Out[31:17], Immediate[16:7], ALUop, Immediate[1:0]}),
    .clk(Clock), .clr(Reset));
  not not_11 (not_11_out, Stall);
  not not_12 (not_12_out, Stall);
  not not_13 (not_13_out, Instruction_Out[30]);
  not not_14 (not_14_out, Instruction_Out[31]);
  and u_Sw (Sw, not_14_out, not_13_out, Instruction_Out[29], Instruction_Out[28], Instruction_Out[27]);
  Register #(.width(32)) register_2 (.D(PC), .en(not_10_out), .Q(PC_OUT), .clk(Clock), .clr(Reset));
  Register #(.width(32)) register_3 (.D(Read1_In), .en(not_11_out), .Q(Read1_Out), .clk(Clock), .clr(Reset));
  Register #(.width(32)) register_4 (.D(Read2_In), .en(not_12_out), .Q(Read2_Out), .clk(Clock), .clr(Reset));
  not not_15 (not_15_out, Instruction_Out[31]);
  not not_16 (not_16_out, Instruction_Out[31]);
  not not_17 (not_17_out, Instruction_Out[29]);
  not not_18 (not_18_out, Instruction_Out[27]);
  not not_19 (not_19_out, Instruction_Out[30]);
  not not_20 (not_20_out, Instruction_Out[28]);
  and u_Lw (Lw, not_15_out, Instruction_Out[30], not_17_out, not_20_out, not_18_out);
  not not_21 (not_21_out, Instruction_Out[28]);
  not not_22 (not_22_out, Instruction_Out[31]);
  not not_23 (not_23_out, Instruction_Out[29]);
  not not_24 (not_24_out, Instruction_Out[29]);
  not not_25 (not_25_out, Instruction_Out[30]);
  and u_J (J, not_16_out, not_19_out, not_24_out, not_21_out, Instruction_Out[27]);
  and u_Bne (Bne, not_22_out, not_25_out, not_23_out, Instruction_Out[28], not_26_out);
  not not_26 (not_26_out, Instruction_Out[27]);
  not not_27 (not_27_out, Instruction_Out[29]);
  not not_28 (not_28_out, Instruction_Out[30]);
  not not_29 (not_29_out, Instruction_Out[31]);
  and u_Jal (Jal, not_29_out, not_28_out, not_27_out, Instruction_Out[28], Instruction_Out[27]);
  not not_30 (not_30_out, Instruction_Out[28]);
  not not_31 (not_31_out, Instruction_Out[27]);
  not not_32 (not_32_out, Instruction_Out[31]);
  not not_33 (not_33_out, Instruction_Out[30]);
  not not_34 (not_34_out, Instruction_Out[30]);
  not not_35 (not_35_out, Instruction_Out[31]);
  and u_Jr (Jr, not_32_out, not_34_out, Instruction_Out[29], not_30_out, not_31_out);
  not not_36 (not_36_out, Instruction_Out[27]);
  not not_37 (not_37_out, Instruction_Out[30]);
  and u_Blt (Blt, not_35_out, not_33_out, Instruction_Out[29], Instruction_Out[28], not_36_out);
  and u_Bex (Bex, Instruction_Out[31], not_37_out, Instruction_Out[29], Instruction_Out[28], not_39_out);
  not not_38 (not_38_out, Instruction_Out[28]);
  not not_39 (not_39_out, Instruction_Out[27]);
  not not_40 (not_40_out, Instruction_Out[30]);
  and u_SetX (SetX, Instruction_Out[31], not_40_out, Instruction_Out[29], not_38_out, Instruction_Out[27]);
  not not_41 (not_41_out, ALUop[3]);
  not not_42 (not_42_out, ALUop[4]);
  and u_Mult (Mult, not_42_out, not_41_out, ALUop[2], ALUop[1], not_43_out);
  not not_43 (not_43_out, ALUop[0]);
  not not_44 (not_44_out, ALUop[3]);
  not not_45 (not_45_out, ALUop[4]);
  and u_Div (Div, not_45_out, not_44_out, ALUop[2], ALUop[1], ALUop[0]);
  or or_1 (ZeroInstruction, Immediate[0], Immediate[1], ALUop[0], ALUop[1], ALUop[2], ALUop[3], ALUop[4], Immediate[7], Immediate[8], Immediate[9], Immediate[10], Immediate[11], Immediate[12], Immediate[13], Immediate[14], Immediate[15], Instruction_Out[17], Instruction_Out[18], Instruction_Out[19], Instruction_Out[20], Instruction_Out[21], Instruction_Out[22], Instruction_Out[23], Instruction_Out[24], Instruction_Out[25], Instruction_Out[26], Instruction_Out[27], Instruction_Out[28], Instruction_Out[29], Instruction_Out[30], Instruction_Out[31], Immediate[16]);

  assign Immediate[6:2] = ALUop;
  assign Instruction_Out[16:0] = {Immediate[16:7], ALUop, Immediate[1:0]};
  assign RD = Instruction_Out[26:22];
  assign RS = Instruction_Out[21:17];
  assign RT = Immediate[16:12];
  assign Shamt = Immediate[11:7];
  assign Target = {Instruction_Out[26:17], Immediate[16:7], ALUop, Immediate[1:0]};

  // Other names for the same wires on the sheet: Opcode[4:0] = Instruction_Out[31:27]
endmodule

module multdiv (
  input  ctrl_mult,
  input  ctrl_div,
  input  clock,
  input  [31:0] DataA,
  input  [31:0] DataB,
  output [31:0] data_result,
  output data_exception,
  output data_resultRDY
);

  wire _1, _2, _4, _8, _16, _32, and_1_out, and_2_out, and_3_out, and_4_out, and_5_out, and_6_out, and_8_out,
       and_9_out, and_10_out, d_ff_1_q, div0, LSB_High32, MSB_Low32, mult_ovf, multiplexer_4_out, nor_1_out,
       not_1_out, not_2_out, not_3_out, not_4_out, not_5_out, not_6_out, not_7_out, not_8_out, not_9_out,
       not_10_out, not_11_out, not_12_out, not_13_out, not_14_out, not_15_out, not_16_out, not_17_out,
       not_18_out, not_19_out, not_20_out, not_21_out, not_22_out, not_23_out, not_24_out, not_25_out,
       not_26_out, not_27_out, not_28_out, not_29_out, not_30_out, not_31_out, not_32_out, not_33_out,
       not_34_out, not_35_out, not_36_out, not_37_out, not_38_out, not_39_out, not_40_out, not_41_out,
       not_42_out, not_43_out, not_44_out, not_45_out, not_46_out, not_47_out, not_48_out, not_49_out,
       not_50_out, not_51_out, not_52_out, not_53_out, not_54_out, not_55_out, not_56_out, not_57_out,
       not_58_out, not_59_out, not_60_out, not_61_out, not_62_out, not_63_out, not_64_out, not_65_out,
       not_66_out, not_67_out, not_68_out, not_69_out, not_70_out, not_71_out, not_72_out, or_1_out,
       or_2_out, or_3_out, or_4_out, or_5_out, RDY_div, RDY_mult, xnor_1_out;
  wire [30:0] result_mult;
  wire [31:0] multiplexer_1_out, result_div;
  wire [31:1] mult_upper;

  not not_1 (not_1_out, LSB_High32);
  not not_2 (not_2_out, mult_upper[1]);
  not not_3 (not_3_out, mult_upper[2]);
  not not_4 (not_4_out, mult_upper[3]);
  not not_5 (not_5_out, mult_upper[4]);
  not not_6 (not_6_out, mult_upper[5]);
  not not_7 (not_7_out, mult_upper[6]);
  not not_8 (not_8_out, mult_upper[7]);
  not not_9 (not_9_out, mult_upper[8]);
  not not_10 (not_10_out, mult_upper[9]);
  not not_11 (not_11_out, mult_upper[10]);
  not not_12 (not_12_out, mult_upper[11]);
  not not_13 (not_13_out, mult_upper[12]);
  not not_14 (not_14_out, mult_upper[13]);
  not not_15 (not_15_out, mult_upper[14]);
  not not_16 (not_16_out, mult_upper[15]);
  not not_17 (not_17_out, mult_upper[16]);
  not not_18 (not_18_out, mult_upper[17]);
  not not_19 (not_19_out, mult_upper[18]);
  not not_20 (not_20_out, mult_upper[19]);
  not not_21 (not_21_out, mult_upper[20]);
  not not_22 (not_22_out, mult_upper[21]);
  not not_23 (not_23_out, mult_upper[22]);
  not not_24 (not_24_out, mult_upper[23]);
  not not_25 (not_25_out, mult_upper[24]);
  not not_26 (not_26_out, mult_upper[25]);
  not not_27 (not_27_out, mult_upper[26]);
  not not_28 (not_28_out, mult_upper[27]);
  not not_29 (not_29_out, mult_upper[28]);
  not not_30 (not_30_out, mult_upper[29]);
  not not_31 (not_31_out, mult_upper[30]);
  not not_32 (not_32_out, mult_upper[31]);
  and and_1 (and_1_out, LSB_High32, mult_upper[1], mult_upper[2], mult_upper[3], mult_upper[4], mult_upper[5], mult_upper[6], mult_upper[7], mult_upper[8], mult_upper[9], mult_upper[10], mult_upper[11], mult_upper[12], mult_upper[13], mult_upper[14], mult_upper[15], mult_upper[17], mult_upper[18], mult_upper[19], mult_upper[20], mult_upper[21], mult_upper[22], mult_upper[23], mult_upper[24], mult_upper[25], mult_upper[26], mult_upper[27], mult_upper[28], mult_upper[29], mult_upper[30], mult_upper[31], mult_upper[16]);
  and and_2 (and_2_out, not_1_out, not_2_out, not_3_out, not_4_out, not_5_out, not_6_out, not_7_out, not_8_out, not_9_out, not_10_out, not_11_out, not_12_out, not_13_out, not_14_out, not_15_out, not_16_out, not_18_out, not_19_out, not_20_out, not_21_out, not_22_out, not_23_out, not_24_out, not_25_out, not_26_out, not_27_out, not_28_out, not_29_out, not_30_out, not_31_out, not_32_out, not_17_out);
  or or_1 (or_1_out, result_mult[0], result_mult[1], result_mult[2], result_mult[3], result_mult[4], result_mult[5], result_mult[6], result_mult[7], result_mult[8], result_mult[9], result_mult[10], result_mult[11], result_mult[12], result_mult[13], result_mult[14], result_mult[15], result_mult[16], result_mult[17], result_mult[18], result_mult[19], result_mult[20], result_mult[21], result_mult[22], result_mult[23], result_mult[24], result_mult[25], result_mult[26], result_mult[27], result_mult[28], result_mult[29], result_mult[30]);
  nor nor_1 (nor_1_out, result_mult[0], result_mult[1], result_mult[2], result_mult[3], result_mult[4], result_mult[5], result_mult[6], result_mult[7], result_mult[8], result_mult[9], result_mult[10], result_mult[11], result_mult[12], result_mult[13], result_mult[14], result_mult[15], result_mult[16], result_mult[17], result_mult[18], result_mult[19], result_mult[20], result_mult[21], result_mult[22], result_mult[23], result_mult[24], result_mult[25], result_mult[26], result_mult[27], result_mult[28], result_mult[29], result_mult[30]);
  Multiplier #(.width(32)) multiplier_1 (
    .a(DataA), .b(DataB), .out({MSB_Low32, result_mult}), .cout({mult_upper, LSB_High32}));  // open: cin
  Divider #(.width(32)) divider_1 (.a(DataA), .b(DataB), .out(result_div));  // open: upper, rem
  xnor xnor_1 (xnor_1_out, LSB_High32, MSB_Low32);
  D_Flip_Flop d_ff_1 (.clk(clock), .D(1'b1), .Q(d_ff_1_q), .en(ctrl_div), .reset(ctrl_mult));  // open: Qn, preset
  and and_3 (and_3_out, MSB_Low32, or_1_out);
  and and_4 (and_4_out, MSB_Low32, nor_1_out);
  Multiplexer #(.width(32), .enable("false")) multiplexer_1 (
    .in0({MSB_Low32, result_mult}), .in1(result_div), .out(multiplexer_1_out), .sel(d_ff_1_q));
  Multiplexer #(.width(32), .enable("false")) multiplexer_2 (
    .in0(multiplexer_1_out), .in1({32{1'b0}}), .out(data_result), .sel(div0));
  Multiplexer #(.enable("false")) multiplexer_3 (.in0(RDY_mult), .in1(RDY_div), .out(data_resultRDY), .sel(d_ff_1_q));
  or or_2 (or_2_out, and_1_out, and_2_out);
  or or_3 (or_3_out, and_3_out, and_4_out);
  not not_33 (not_33_out, _16);
  not not_34 (not_34_out, _8);
  not not_35 (not_35_out, _4);
  not not_36 (not_36_out, _2);
  not not_37 (not_37_out, _32);
  not not_38 (not_38_out, _8);
  not not_39 (not_39_out, _4);
  not not_40 (not_40_out, _2);
  T_Flip_Flop t_ff_1 (.clk(clock), .T(1'b1), .Q(_1), .reset(or_4_out), .en(1'b1));  // open: Qn, preset
  or or_4 (or_4_out, ctrl_mult, ctrl_div);
  or or_5 (or_5_out, xnor_1_out, or_3_out);
  and LASTD (RDY_div, _32, not_33_out, not_34_out, not_35_out, not_36_out, _1);
  and LASTM (RDY_mult, not_37_out, _16, not_38_out, not_39_out, not_40_out, _1);
  and and_5 (and_5_out, 1'b1, _1);
  T_Flip_Flop t_ff_2 (.clk(clock), .T(and_5_out), .Q(_2), .reset(or_4_out), .en(1'b1));  // open: Qn, preset
  not not_41 (not_41_out, DataB[0]);
  not not_42 (not_42_out, DataB[1]);
  not not_43 (not_43_out, DataB[2]);
  not not_44 (not_44_out, DataB[3]);
  not not_45 (not_45_out, DataB[4]);
  not not_46 (not_46_out, DataB[5]);
  not not_47 (not_47_out, DataB[6]);
  not not_48 (not_48_out, DataB[7]);
  not not_49 (not_49_out, DataB[8]);
  not not_50 (not_50_out, DataB[9]);
  not not_51 (not_51_out, DataB[10]);
  not not_52 (not_52_out, DataB[11]);
  not not_53 (not_53_out, DataB[12]);
  not not_54 (not_54_out, DataB[13]);
  not not_55 (not_55_out, DataB[14]);
  not not_56 (not_56_out, DataB[15]);
  not not_57 (not_57_out, DataB[16]);
  not not_58 (not_58_out, DataB[17]);
  not not_59 (not_59_out, DataB[18]);
  not not_60 (not_60_out, DataB[19]);
  not not_61 (not_61_out, DataB[20]);
  not not_62 (not_62_out, DataB[21]);
  not not_63 (not_63_out, DataB[22]);
  not not_64 (not_64_out, DataB[23]);
  not not_65 (not_65_out, DataB[24]);
  not not_66 (not_66_out, DataB[25]);
  not not_67 (not_67_out, DataB[26]);
  not not_68 (not_68_out, DataB[27]);
  not not_69 (not_69_out, DataB[28]);
  not not_70 (not_70_out, DataB[29]);
  not not_71 (not_71_out, DataB[30]);
  not not_72 (not_72_out, DataB[31]);
  and and_6 (and_6_out, and_5_out, _2);
  and and_7 (div0, not_41_out, not_42_out, not_43_out, not_44_out, not_45_out, not_46_out, not_47_out, not_48_out, not_49_out, not_50_out, not_51_out, not_52_out, not_53_out, not_54_out, not_55_out, not_56_out, not_58_out, not_59_out, not_60_out, not_61_out, not_62_out, not_63_out, not_64_out, not_65_out, not_66_out, not_67_out, not_68_out, not_69_out, not_70_out, not_71_out, not_72_out, not_57_out);
  T_Flip_Flop t_ff_3 (.clk(clock), .T(and_6_out), .Q(_4), .reset(or_4_out), .en(1'b1));  // open: Qn, preset
  and and_8 (and_8_out, and_6_out, _4);
  Multiplexer #(.enable("false")) multiplexer_4 (.in0(1'b0), .in1(div0), .out(multiplexer_4_out), .sel(d_ff_1_q));
  and and_9 (and_9_out, and_8_out, _8);
  T_Flip_Flop t_ff_4 (.clk(clock), .T(and_8_out), .Q(_8), .reset(or_4_out), .en(1'b1));  // open: Qn, preset
  nand nand_1 (mult_ovf, or_2_out, or_5_out);
  or or_6 (data_exception, multiplexer_4_out, mult_ovf);
  and and_10 (and_10_out, and_9_out, _16);
  T_Flip_Flop t_ff_5 (.clk(clock), .T(and_9_out), .Q(_16), .reset(or_4_out), .en(1'b1));  // open: Qn, preset
  T_Flip_Flop t_ff_6 (.clk(clock), .T(and_10_out), .Q(_32), .reset(or_4_out), .en(1'b1));  // open: Qn, preset

  // Other names for the same wires on the sheet: clk = clock; Divisor[31:0] = DataB; mult_upper[0] = LSB_High32;
  //   result_mult[31] = MSB_Low32
endmodule

module MW_Module (
  input  [31:0] PC,
  input  Stall,
  input  [31:0] Target_In,
  input  Clock,
  input  Reset,
  input  [31:0] Instruction,
  input  [31:0] Data_In,
  output [31:0] PC_OUT,
  output [31:0] Target_Out,
  output [4:0] ALUOp,
  output [4:0] Destination_Reg,
  output RD_Is_Zero_Register,
  output [4:0] OpCode,
  output [31:0] Data_to_write,
  output ModifiesRD_MW,
  output SetX_MW,
  output LW_MW,
  output JAL_MW,
  output WEnable
);

  wire Addi_out, not_1_out, not_2_out, not_3_out, not_4_out, not_5_out, not_6_out, not_7_out, not_8_out,
       not_9_out, not_10_out, not_11_out, not_12_out, not_13_out, not_14_out, not_15_out, not_16_out,
       not_17_out, not_18_out, not_19_out, not_20_out, not_21_out, not_22_out, not_23_out, not_24_out,
       not_25_out, not_26_out, RType;
  wire [21:0] register_1_q;

  not not_1 (not_1_out, OpCode[4]);
  not not_2 (not_2_out, OpCode[0]);
  not not_3 (not_3_out, OpCode[2]);
  not not_4 (not_4_out, OpCode[3]);
  not not_5 (not_5_out, OpCode[1]);
  and R_Type (RType, not_1_out, not_4_out, not_3_out, not_5_out, not_2_out);
  not not_6 (not_6_out, Stall);
  not not_7 (not_7_out, OpCode[4]);
  not not_8 (not_8_out, OpCode[3]);
  not not_9 (not_9_out, OpCode[1]);
  not not_10 (not_10_out, OpCode[4]);
  and Addi (Addi_out, not_10_out, not_8_out, OpCode[2], not_9_out, OpCode[0]);
  not not_11 (not_11_out, Stall);
  Register #(.width(32)) register_1 (
    .D(Instruction), .en(not_6_out),
    .Q({OpCode, Destination_Reg, register_1_q[21:7], ALUOp, register_1_q[1:0]}), .clk(Clock), .clr(Reset));
  // Probe on {OpCode, Destination_Reg, register_1_q[21:7], ALUOp, register_1_q[1:0]}
  not not_12 (not_12_out, Stall);
  not not_13 (not_13_out, OpCode[4]);
  not not_14 (not_14_out, OpCode[2]);
  not not_15 (not_15_out, OpCode[3]);
  not not_16 (not_16_out, OpCode[1]);
  not not_17 (not_17_out, OpCode[0]);
  not not_18 (not_18_out, OpCode[2]);
  and Lw (LW_MW, not_7_out, OpCode[3], not_18_out, not_16_out, not_17_out);
  and Jal (JAL_MW, not_13_out, not_15_out, not_14_out, OpCode[1], OpCode[0]);
  or or_1 (WEnable, RType, Addi_out, LW_MW, JAL_MW, SetX_MW);
  Register #(.width(32)) register_2 (.D(PC), .en(not_11_out), .Q(PC_OUT), .clk(Clock), .clr(Reset));
  Register #(.width(32)) register_3 (.D(Data_In), .en(not_12_out), .Q(Data_to_write), .clk(Clock), .clr(Reset));
  not not_19 (not_19_out, OpCode[1]);
  not not_20 (not_20_out, OpCode[3]);
  and SetX (SetX_MW, OpCode[4], not_20_out, OpCode[2], not_19_out, OpCode[0]);
  not not_21 (not_21_out, Destination_Reg[0]);
  not not_22 (not_22_out, Destination_Reg[1]);
  not not_23 (not_23_out, Destination_Reg[2]);
  not not_24 (not_24_out, Destination_Reg[3]);
  not not_25 (not_25_out, Destination_Reg[4]);
  and and_1 (RD_Is_Zero_Register, not_21_out, not_22_out, not_23_out, not_24_out, not_25_out);
  or or_2 (ModifiesRD_MW, RType, Addi_out, LW_MW, SetX_MW);
  not not_26 (not_26_out, Stall);
  Register #(.width(32)) register_4 (.D(Target_In), .en(not_26_out), .Q(Target_Out), .clk(Clock), .clr(Reset));

  // Other names for the same wires on the sheet: Rd[4:0] = Destination_Reg
endmodule

module XM_Module (
  input  [31:0] PC,
  input  [31:0] Read1_DX,
  input  [31:0] ALU_Output,
  input  ovf,
  input  MultOvf,
  input  Stall,
  input  Clock,
  input  Reset,
  input  [4:0] ALUOpDX,
  input  [31:0] Instruction,
  input  [31:0] Target_In,
  output [31:0] PC_OUT,
  output [31:0] Read1_XM,
  output [31:0] ALU_Out_XM,
  output [31:0] Instruction_Out,
  output [4:0] RD_XM,
  output RD_Is_Zero_Register,
  output [4:0] ALUOP,
  output [4:0] Opcode,
  output [31:0] Target_Out,
  output Sw,
  output Lw,
  output JAL,
  output SetX,
  output ModifiesRD
);

  wire Addi_out, comparator_1_eq, J_Type_out, not_1_out, not_2_out, not_3_out, not_4_out, not_5_out,
       not_6_out, not_7_out, not_8_out, not_9_out, not_10_out, not_11_out, not_12_out, not_13_out,
       not_14_out, not_15_out, not_16_out, not_17_out, not_18_out, not_19_out, not_20_out, not_21_out,
       not_22_out, not_23_out, not_24_out, not_25_out, not_26_out, not_27_out, not_28_out, not_29_out,
       or_1_out, or_3_out;
  wire [4:0] multiplexer_1_out;
  wire [31:0] multiplexer_2_out, multiplexer_3_out, multiplexer_4_out;

  or or_1 (or_1_out, ovf, MultOvf);
  Multiplexer #(.width(5), .enable("false")) multiplexer_1 (
    .in0(Instruction[26:22]), .in1(5'b11110), .out(multiplexer_1_out), .sel(or_1_out));
  not not_1 (not_1_out, Instruction_Out[30]);
  not not_2 (not_2_out, Instruction_Out[31]);
  and u_Sw (Sw, not_2_out, not_1_out, Instruction_Out[29], Instruction_Out[28], Instruction_Out[27]);
  not not_3 (not_3_out, Stall);
  not not_4 (not_4_out, Stall);
  Register #(.width(32)) register_1 (
    .D({Instruction[31:27], multiplexer_1_out, Instruction[21:0]}), .en(not_5_out),
    .Q({Instruction_Out[31:7], ALUOP, Instruction_Out[1:0]}), .clk(Clock), .clr(Reset));
  not not_5 (not_5_out, Stall);
  not not_6 (not_6_out, Instruction_Out[28]);
  not not_7 (not_7_out, Instruction_Out[29]);
  not not_8 (not_8_out, Instruction_Out[27]);
  not not_9 (not_9_out, Instruction_Out[31]);
  and u_Lw (Lw, not_9_out, Instruction_Out[30], not_7_out, not_6_out, not_8_out);
  Register #(.width(32)) register_2 (.D(PC), .en(not_3_out), .Q(PC_OUT), .clk(Clock), .clr(Reset));
  Register #(.width(32)) register_3 (.D(Read1_DX), .en(not_4_out), .Q(Read1_XM), .clk(Clock), .clr(Reset));
  not not_10 (not_10_out, Instruction_Out[28]);
  not not_11 (not_11_out, Instruction_Out[31]);
  not not_12 (not_12_out, Instruction_Out[30]);
  not not_13 (not_13_out, Instruction_Out[30]);
  and u_SetX (SetX, Instruction_Out[31], not_13_out, Instruction_Out[29], not_10_out, Instruction_Out[27]);
  Multiplexer #(.select(3), .width(32), .enable("false")) multiplexer_2 (
    .in0(32'h1), .in1(32'h3), .in2({32{1'b0}}), .in3({32{1'b0}}), .in4({32{1'b0}}), .in5({32{1'b0}}),
    .in6(32'h4), .in7(32'h5), .out(multiplexer_2_out), .sel(ALUOpDX[2:0]));
  not not_14 (not_14_out, Instruction_Out[30]);
  not not_15 (not_15_out, Instruction_Out[29]);
  not not_16 (not_16_out, Instruction_Out[29]);
  not not_17 (not_17_out, Instruction_Out[31]);
  not not_18 (not_18_out, Instruction_Out[28]);
  and u_JAL (JAL, not_11_out, not_12_out, not_16_out, Instruction_Out[28], Instruction_Out[27]);
  and J_Type (J_Type_out, not_17_out, not_14_out, not_15_out, not_18_out, not_21_out);
  Comparator #(.width(5)) comparator_1 (.a(ALUOpDX), .b(5'b00101), .eq(comparator_1_eq));  // open: gt, lt
  not not_19 (not_19_out, Instruction_Out[31]);
  not not_20 (not_20_out, Instruction_Out[30]);
  not not_21 (not_21_out, Instruction_Out[27]);
  not not_22 (not_22_out, Instruction_Out[28]);
  and Addi (Addi_out, not_19_out, not_20_out, Instruction_Out[29], not_22_out, Instruction_Out[27]);
  Multiplexer #(.width(32), .enable("false")) multiplexer_3 (
    .in0(multiplexer_2_out), .in1(32'h2), .out(multiplexer_3_out), .sel(comparator_1_eq));
  or or_2 (ModifiesRD, Lw, Addi_out, J_Type_out, SetX);
  Multiplexer #(.width(32), .enable("false")) multiplexer_4 (
    .in0(ALU_Output), .in1(multiplexer_3_out), .out(multiplexer_4_out), .sel(or_3_out));
  or or_3 (or_3_out, ovf, MultOvf);
  not not_23 (not_23_out, Stall);
  not not_24 (not_24_out, Stall);
  Register #(.width(32)) register_4 (.D(Target_In), .en(not_23_out), .Q(Target_Out), .clk(Clock), .clr(Reset));
  Register #(.width(32)) register_5 (.D(multiplexer_4_out), .en(not_24_out), .Q(ALU_Out_XM), .clk(Clock), .clr(Reset));
  not not_25 (not_25_out, Instruction_Out[22]);
  not not_26 (not_26_out, Instruction_Out[23]);
  not not_27 (not_27_out, Instruction_Out[24]);
  not not_28 (not_28_out, Instruction_Out[25]);
  not not_29 (not_29_out, Instruction_Out[26]);
  and and_1 (RD_Is_Zero_Register, not_25_out, not_26_out, not_27_out, not_28_out, not_29_out);

  assign Instruction_Out[6:2] = ALUOP;
  assign Opcode = Instruction_Out[31:27];
  assign RD_XM = Instruction_Out[26:22];

  // Other names for the same wires on the sheet: ALUOp_t[4:0] = ALUOpDX; ALUOvf = ovf
endmodule
module full_processor_12 (
  input  in_1,
  input  Global_Reset,
  input  [4:0] _31_27_OP,
  input  [4:0] _26_22_RD,
  input  [4:0] _21_17_RS,
  input  [4:0] _16_12_RT,
  input  [31:0] NoOp,
  input  [4:0] _11_7_SHAMT,
  input  [4:0] _6_2_ALUOP,
  input  [1:0] _1_0_ZERO
);

  wire Addi_DX, Addi_FD, ALU_ILT, ALU_INE, ALU_Ovf, ALU_Ovf_MW, ALU_Ovf_XM, and_1_out, and_2_out, and_3_out,
       and_5_out, and_6_out, and_7_out, and_8_out, and_9_out, and_10_out, and_11_out, and_12_out, and_13_out,
       and_14_out, and_15_out, and_16_out, and_17_out, and_18_out, and_19_out, and_20_out, and_21_out,
       and_22_out, and_27_out, and_28_out, and_29_out, and_30_out, and_31_out, and_32_out, and_33_out,
       and_34_out, and_35_out, and_36_out, and_39_out, and_40_out, and_41_out, and_42_out, and_43_out,
       and_44_out, and_45_out, and_46_out, and_48_out, and_49_out, and_50_out, and_51_out, and_52_out,
       and_53_out, and_54_out, and_55_out, BEX_DX, Bex_FD, BEX_MW_BYPASS, BEX_NE, BEX_SETX_BYPASS_MW,
       BEX_SETX_BYPASS_XM, BEX_XM_BYPASS, BLT_DX, BNE_DX, Branch_FD, comparator_1_eq, comparator_2_eq,
       comparator_3_eq, comparator_4_eq, comparator_5_eq, comparator_6_eq, comparator_7_eq, comparator_8_eq,
       comparator_9_eq, comparator_10_eq, comparator_11_eq, comparator_12_eq, comparator_13_eq,
       comparator_14_eq, comparator_15_eq, comparator_16_eq, comparator_17_eq, comparator_18_eq,
       comparator_19_eq, comparator_20_eq, comparator_21_eq, comparator_22_gt, comparator_22_lt,
       comparator_23_eq, comparator_24_eq, comparator_25_eq, comparator_26_eq, comparator_27_eq,
       comparator_28_eq, comparator_29_eq, comparator_30_eq, comparator_31_eq, comparator_32_eq,
       comparator_33_eq, comparator_34_eq, comparator_35_eq, comparator_36_eq, comparator_37_eq,
       comparator_38_eq, comparator_39_eq, comparator_40_eq, comparator_41_eq, comparator_42_eq, Div_DX,
       div_ongoing, Div_Ongoing_q, div_start, fall, J_DX, JAL_DX, JAL_MW, JAL_MW_R1_Bypass, JAL_MW_R2_Bypass,
       JAL_XM, JAL_XM_R1_Bypass, JAL_XM_R2_Bypass, JR_DX, LW_DX, LW_MW, LW_R1_STALL, LW_SW_Bypass, LW_XM,
       ModifiesRD_MW, ModifiesRD_XM, Mult_DX, mult_ongoing, Mult_Ongoing_q, mult_start, multdiv_ovf,
       multdiv_rdy, multiplexer_31_out, MW_R1_Bypass, MW_R2_Bypass, MW_RD_IS_0, NOOP_DX, NoOp_DX_t, NOOP_t,
       not_1_out, not_3_out, not_4_out, not_5_out, not_6_out, not_7_out, not_8_out, not_9_out, not_10_out,
       not_11_out, not_12_out, or_3_out, or_4_out, or_5_out, or_6_out, or_7_out, or_15_out, or_16_out,
       or_17_out, or_18_out, or_19_out, or_25_out, or_26_out, or_27_out, or_28_out, or_29_out, or_36_out,
       or_37_out, or_38_out, rise, rstatus_r1_MW_bypass, rstatus_r1_XM_bypass, rstatus_r2_MW_bypass,
       rstatus_r2_XM_bypass, RType_DX, Rtype_FD, SETX_DX, SetX_MW, SETX_MW_R1_Bypass, SETX_MW_R2_Bypass,
       SetX_XM, SETX_XM_R1_Bypass, SETX_XM_R2_Bypass, Stall_DX, Stall_FD, Stall_PC, SW_DX, SW_XM, WEn_mw,
       XM_R1_Bypass, XM_R2_Bypass, XM_RD_IS_0;
  wire [4:0] ALU_Op_MW, ALUOp, ALUOp_XM, final_reg_dest, multiplexer_3_out, multiplexer_4_out,
       multiplexer_5_out, multiplexer_6_out, multiplexer_7_out, multiplexer_32_out, multiplexer_36_out,
       OpCode_MW, Opcode_XM, RD_DX, RD_FD, RD_MW, RD_XM, RS_DX, RS_FD, RT_DX, RT_FD, Shamt;
  wire [16:0] Immediate_17;
  wire [26:0] Target_DX;
  wire [31:0] ALU_XM, ALUOut, data_out_mw, data_to_write, final_data_out, Immediate_32, Instr_DX, Instr_FD,
       Instr_XM, multdiv_result, multiplexer_1_out, multiplexer_2_out, multiplexer_8_out, multiplexer_9_out,
       multiplexer_10_out, multiplexer_11_out, multiplexer_12_out, multiplexer_13_out, multiplexer_14_out,
       multiplexer_15_out, multiplexer_16_out, multiplexer_17_out, multiplexer_18_out, multiplexer_19_out,
       multiplexer_20_out, multiplexer_21_out, multiplexer_22_out, multiplexer_23_out, multiplexer_24_out,
       multiplexer_25_out, multiplexer_26_out, multiplexer_27_out, multiplexer_28_out, multiplexer_29_out,
       multiplexer_30_out, multiplexer_33_out, multiplexer_34_out, multiplexer_35_out, multiplexer_37_out,
       multiplexer_38_out, multiplexer_39_out, multiplexer_40_out, multiplexer_41_out, multiplexer_42_out,
       multiplexer_43_out, multiplexer_46_out, multiplexer_47_out, multiplexer_49_out, multiplexer_50_out,
       multiplexer_53_out, multiplexer_54_out, n32_bit_carry_lookahead_3_s, ovf_override_value,
       ovf_override_value_2, PC, PC_1, PC_DX, PC_DX_1, PC_FD, PC_MW, PC_MW_1, PC_XM, PC_XM_1, ram_1_data,
       Read1_DX, Read1_XM, Read2_DX, ReadA, ReadB, real_alu_in1, real_alu_in2, Target_DX_Extended, Target_MW,
       Target_XM_Extended;

  Register #(.width(32)) PC_REG (.D(multiplexer_24_out), .en(not_1_out), .Q(PC), .clk(rise), .clr(Global_Reset));
  not not_1 (not_1_out, Stall_PC);
  Clock Global_Clk (.out(rise));
  // Probe on PC
  not not_2 (fall, rise);
  and and_1 (and_1_out, BLT_DX, ALU_ILT);
  and and_2 (and_2_out, BEX_NE, BEX_DX);
  and and_3 (and_3_out, BNE_DX, ALU_INE);
  ROM #(.addrWidth(12), .dataWidth(32)) rom_1 (.addr(PC[11:0]));  // open: data, sel
  Multiplexer #(.width(32), .enable("false")) multiplexer_1 (
    .in0({_31_27_OP, _26_22_RD, _21_17_RS, _16_12_RT, _11_7_SHAMT, _6_2_ALUOP, _1_0_ZERO}), .in1(NoOp),
    .out(multiplexer_1_out), .sel(in_1));
  _32_bit_carry_lookahead u_32_bit_carry_lookahead_1 (.A_32(PC), .B_32(32'h1), .C0(1'b0), .S(PC_1));  // open: Overflow
  or or_1 (NOOP_DX, LW_R1_STALL, and_3_out, J_DX, and_1_out, JR_DX, JAL_DX, and_2_out);
  or or_2 (NOOP_t, J_DX, and_3_out, and_1_out, JR_DX, JAL_DX, and_2_out);
  // Probe on {_31_27_OP, _26_22_RD, _21_17_RS, _16_12_RT, _11_7_SHAMT, _6_2_ALUOP, _1_0_ZERO}
  Multiplexer #(.width(32), .enable("false")) multiplexer_2 (
    .in0(multiplexer_1_out), .in1({32{1'b0}}), .out(multiplexer_2_out), .sel(NOOP_t));
  FD_Module fd_module_1 (
    .Instruction(multiplexer_2_out), .Stall(Stall_FD), .Clock(rise), .Reset(Global_Reset),
    .Instruction_FD(Instr_FD), .Rt(RT_FD), .Rs(RS_FD), .Rd(RD_FD), .PC(PC), .PC_OUT(PC_FD),
    .R_Type(Rtype_FD), .Bex(Bex_FD), .Addi(Addi_FD), .Branch(Branch_FD));  // open: JR
  or or_3 (or_3_out, RType_DX, JR_DX, SW_DX, Addi_DX);
  Multiplexer #(.width(5), .enable("false")) multiplexer_3 (
    .in0(RD_FD), .in1(5'b11110), .out(multiplexer_3_out), .sel(Bex_FD));
  or or_4 (or_4_out, div_ongoing, mult_ongoing);
  not not_3 (not_3_out, multdiv_rdy);
  or or_5 (or_5_out, Rtype_FD, Addi_FD);
  or or_6 (or_6_out, BNE_DX, BLT_DX);
  Multiplexer #(.width(5), .enable("false")) multiplexer_4 (
    .in0(multiplexer_3_out), .in1(RS_FD), .out(multiplexer_4_out), .sel(Rtype_FD));
  Multiplexer #(.width(5), .enable("false")) multiplexer_5 (
    .in0(RS_FD), .in1(RT_FD), .out(multiplexer_5_out), .sel(Rtype_FD));
  and and_4 (Stall_DX, or_4_out, not_3_out);
  Comparator #(.width(5)) comparator_1 (.a(RD_DX), .b(RS_FD), .eq(comparator_1_eq));  // open: gt, lt
  Comparator #(.width(5)) comparator_2 (.a(RD_DX), .b(RT_FD), .eq(comparator_2_eq));  // open: gt, lt
  Comparator #(.width(5)) comparator_3 (.a(RD_DX), .b(RD_FD), .eq(comparator_3_eq));  // open: gt, lt
  Comparator #(.width(5)) comparator_4 (.a(RS_DX), .b(5'b11110), .eq(comparator_4_eq));  // open: gt, lt
  Comparator #(.width(5)) comparator_5 (.a(RS_DX), .b(5'b11110), .eq(comparator_5_eq));  // open: gt, lt
  Comparator #(.width(5)) comparator_6 (.a(RT_DX), .b(5'b11110), .eq(comparator_6_eq));  // open: gt, lt
  Comparator #(.width(5)) comparator_7 (.a(RT_DX), .b(5'b11110), .eq(comparator_7_eq));  // open: gt, lt
  Comparator #(.width(5)) comparator_8 (.a(RD_DX), .b(5'b11110), .eq(comparator_8_eq));  // open: gt, lt
  or or_7 (or_7_out, BNE_DX, JR_DX, BLT_DX);
  Comparator #(.width(5)) comparator_9 (.a(RD_DX), .b(5'b11110), .eq(comparator_9_eq));  // open: gt, lt
  Comparator #(.width(5)) comparator_10 (.a(RS_DX), .b(5'b11110), .eq(comparator_10_eq));  // open: gt, lt
  Comparator #(.width(5)) comparator_11 (.a(RS_DX), .b(5'b11110), .eq(comparator_11_eq));  // open: gt, lt
  Multiplexer #(.width(5), .enable("false")) multiplexer_6 (
    .in0(multiplexer_7_out), .in1(5'b11110), .out(multiplexer_6_out), .sel(SetX_MW));
  or or_8 (Stall_PC, LW_R1_STALL, Stall_DX);
  or or_9 (Stall_FD, LW_R1_STALL, Stall_DX);
  and and_5 (and_5_out, comparator_4_eq, or_3_out, SetX_XM);
  and and_6 (and_6_out, comparator_5_eq, or_3_out, SetX_MW);
  and and_7 (and_7_out, RType_DX, comparator_6_eq, SetX_XM);
  and and_8 (and_8_out, RType_DX, comparator_7_eq, SetX_MW);
  and and_9 (and_9_out, comparator_8_eq, SetX_XM, or_7_out);
  and and_10 (and_10_out, or_7_out, SetX_MW, comparator_9_eq);
  and and_11 (and_11_out, comparator_10_eq, SetX_XM, or_6_out);
  and and_12 (and_12_out, or_6_out, SetX_MW, comparator_11_eq);
  Multiplexer #(.width(5), .enable("false")) multiplexer_7 (
    .in0(final_reg_dest), .in1({5{1'b1}}), .out(multiplexer_7_out), .sel(JAL_MW));
  Multiplexer #(.width(32), .enable("false")) multiplexer_8 (
    .in0(multiplexer_9_out), .in1(Target_MW), .out(multiplexer_8_out), .sel(SetX_MW));
  and and_13 (and_13_out, or_5_out, comparator_1_eq, LW_DX);
  and and_14 (and_14_out, Rtype_FD, comparator_2_eq, LW_DX);
  and and_15 (and_15_out, Branch_FD, comparator_3_eq, LW_DX);
  Multiplexer #(.width(32), .enable("false")) multiplexer_9 (
    .in0(final_data_out), .in1(PC_MW_1), .out(multiplexer_9_out), .sel(JAL_MW));
  register_files register_files_1 (
    .data_writeReg(multiplexer_8_out), .clk(fall), .ctrl_reset(Global_Reset), .ctrl_writeEnable(WEn_mw),
    .ctrl_writeReg(multiplexer_6_out), .ctrl_readRegA(multiplexer_4_out), .ctrl_readRegB(multiplexer_5_out),
    .data_readRegA(ReadA), .data_readRegB(ReadB));
  or or_10 (LW_R1_STALL, and_13_out, and_14_out, and_15_out);
  or or_11 (SETX_XM_R1_Bypass, and_5_out, and_9_out);
  or or_12 (SETX_MW_R1_Bypass, and_6_out, and_10_out);
  or or_13 (SETX_XM_R2_Bypass, and_7_out, and_11_out);
  or or_14 (SETX_MW_R2_Bypass, and_8_out, and_12_out);
  Multiplexer #(.width(32), .enable("false")) multiplexer_10 (
    .in0(Read1_DX), .in1(data_out_mw), .out(multiplexer_10_out), .sel(BEX_MW_BYPASS));
  _32_bit_carry_lookahead u_32_bit_carry_lookahead_2 (
    .A_32(PC_DX), .B_32(32'h1), .C0(1'b0), .S(PC_DX_1));  // open: Overflow
  Multiplexer #(.width(32), .enable("false")) multiplexer_11 (
    .in0(Instr_FD), .in1({32{1'b0}}), .out(multiplexer_11_out), .sel(NOOP_DX));
  Multiplexer #(.width(32), .enable("false")) multiplexer_12 (
    .in0(ReadA), .in1({32{1'b0}}), .out(multiplexer_12_out), .sel(NOOP_DX));
  Multiplexer #(.width(32), .enable("false")) multiplexer_13 (
    .in0(ReadB), .in1({32{1'b0}}), .out(multiplexer_13_out), .sel(NOOP_DX));
  or or_15 (or_15_out, J_DX, JAL_DX, and_16_out);
  DX_Module dx_module_1 (
    .Stall(Stall_DX), .PC(PC_FD), .Clock(rise), .Reset(Global_Reset), .Instruction(multiplexer_11_out),
    .Read1_In(multiplexer_12_out), .Read2_In(multiplexer_13_out), .PC_OUT(PC_DX), .Instruction_Out(Instr_DX),
    .ALUop(ALUOp), .Shamt(Shamt), .Immediate(Immediate_17), .Read1_Out(Read1_DX), .Read2_Out(Read2_DX),
    .R_Type(RType_DX), .Addi(Addi_DX), .Sw(SW_DX), .Lw(LW_DX), .J(J_DX), .Bne(BNE_DX), .Jal(JAL_DX),
    .Blt(BLT_DX), .Bex(BEX_DX), .SetX(SETX_DX), .Mult(Mult_DX), .Div(Div_DX), .Target(Target_DX), .RS(RS_DX),
    .RT(RT_DX), .ZeroInstruction(NoOp_DX_t), .RD(RD_DX), .Jr(JR_DX));
  Multiplexer #(.width(32), .enable("false")) multiplexer_14 (
    .in0(multiplexer_10_out), .in1(data_to_write), .out(multiplexer_14_out), .sel(BEX_XM_BYPASS));
  Multiplexer #(.width(32), .enable("false")) multiplexer_15 (
    .in0(PC_1), .in1(Target_DX_Extended), .out(multiplexer_15_out), .sel(or_15_out));
  and and_16 (and_16_out, BEX_NE, BEX_DX);
  _32_bit_carry_lookahead u_32_bit_carry_lookahead_3 (
    .A_32(PC_DX_1), .B_32(Immediate_32), .C0(1'b0), .S(n32_bit_carry_lookahead_3_s));  // open: Overflow
  Multiplexer #(.width(32), .enable("false")) multiplexer_16 (
    .in0(multiplexer_14_out), .in1(Target_MW), .out(multiplexer_16_out), .sel(BEX_SETX_BYPASS_MW));
  or or_16 (or_16_out, BNE_DX, BLT_DX);
  Multiplexer #(.width(32), .enable("false")) multiplexer_17 (
    .in0(multiplexer_15_out), .in1(n32_bit_carry_lookahead_3_s), .out(multiplexer_17_out), .sel(or_17_out));
  or or_17 (or_17_out, and_17_out, and_18_out);
  and and_17 (and_17_out, BNE_DX, ALU_INE);
  and and_18 (and_18_out, ALU_ILT, BLT_DX);
  Comparator #(.width(5)) comparator_12 (.a(RS_DX), .b(RD_XM), .eq(comparator_12_eq));  // open: gt, lt
  or or_18 (or_18_out, RType_DX, JR_DX, SW_DX, Addi_DX);
  not not_4 (not_4_out, XM_RD_IS_0);
  Comparator #(.width(5)) comparator_13 (.a(RS_DX), .b(RD_MW), .eq(comparator_13_eq));  // open: gt, lt
  not not_5 (not_5_out, MW_RD_IS_0);
  Comparator #(.width(5)) comparator_14 (.a(RT_DX), .b(RD_XM), .eq(comparator_14_eq));  // open: gt, lt
  not not_6 (not_6_out, XM_RD_IS_0);
  not not_7 (not_7_out, Addi_DX);
  Comparator #(.width(5)) comparator_15 (.a(RT_DX), .b(RD_MW), .eq(comparator_15_eq));  // open: gt, lt
  not not_8 (not_8_out, MW_RD_IS_0);
  not not_9 (not_9_out, Addi_DX);
  Comparator #(.width(5)) comparator_16 (.a(RD_DX), .b(RD_XM), .eq(comparator_16_eq));  // open: gt, lt
  or or_19 (or_19_out, BNE_DX, JR_DX, BLT_DX);
  Comparator #(.width(5)) comparator_17 (.a(RD_DX), .b(RD_MW), .eq(comparator_17_eq));  // open: gt, lt
  Comparator #(.width(5)) comparator_18 (.a(RS_DX), .b(RD_XM), .eq(comparator_18_eq));  // open: gt, lt
  Comparator #(.width(5)) comparator_19 (.a(RS_DX), .b(RD_MW), .eq(comparator_19_eq));  // open: gt, lt
  Comparator #(.width(5)) comparator_20 (.a(RD_XM), .b(5'b11110), .eq(comparator_20_eq));  // open: gt, lt
  Comparator #(.width(5)) comparator_21 (.a(RD_MW), .b(5'b11110), .eq(comparator_21_eq));  // open: gt, lt
  Multiplexer #(.width(32), .enable("false")) multiplexer_18 (
    .in0(multiplexer_16_out), .in1(Target_XM_Extended), .out(multiplexer_18_out), .sel(BEX_SETX_BYPASS_XM));
  and and_19 (and_19_out, comparator_16_eq, ModifiesRD_XM, or_19_out);
  and and_20 (and_20_out, or_19_out, ModifiesRD_XM, comparator_17_eq);
  and and_21 (and_21_out, comparator_18_eq, ModifiesRD_XM, or_16_out);
  and and_22 (and_22_out, or_16_out, ModifiesRD_MW, comparator_19_eq);
  and and_23 (BEX_XM_BYPASS, comparator_20_eq, ModifiesRD_XM, BEX_DX);
  and and_24 (BEX_MW_BYPASS, BEX_DX, ModifiesRD_MW, comparator_21_eq);
  and and_25 (BEX_SETX_BYPASS_XM, SetX_XM, BEX_DX);
  and and_26 (BEX_SETX_BYPASS_MW, SetX_MW, BEX_DX);
  Multiplexer #(.width(32), .enable("false")) multiplexer_19 (
    .in0(multiplexer_17_out), .in1(Read1_DX), .out(multiplexer_19_out), .sel(JR_DX));
  assign Immediate_32 = {{15{1'b0}}, Immediate_17};  // Bit_Extender bit_extender_1
  assign Target_DX_Extended = {{5{1'b0}}, Target_DX};  // Bit_Extender bit_extender_2
  Comparator #(.width(32)) comparator_22 (
    .a(multiplexer_18_out), .b({32{1'b0}}), .gt(comparator_22_gt), .lt(comparator_22_lt));  // open: eq
  and and_27 (and_27_out, comparator_12_eq, NoOp_DX_t, ModifiesRD_XM, or_18_out, not_4_out);
  and and_28 (and_28_out, or_18_out, NoOp_DX_t, ModifiesRD_MW, comparator_13_eq, not_5_out);
  and and_29 (and_29_out, comparator_14_eq, NoOp_DX_t, not_7_out, RType_DX, not_6_out, ModifiesRD_XM);
  and and_30 (and_30_out, RType_DX, NoOp_DX_t, not_9_out, comparator_15_eq, not_8_out, ModifiesRD_MW);
  Multiplexer #(.width(32), .enable("false")) multiplexer_20 (
    .in0(multiplexer_19_out), .in1(PC_XM_1), .out(multiplexer_20_out), .sel(and_31_out));
  and and_31 (and_31_out, JR_DX, JAL_XM);
  or or_20 (BEX_NE, comparator_22_gt, comparator_22_lt);
  or or_21 (XM_R1_Bypass, and_27_out, and_19_out);
  or or_22 (MW_R1_Bypass, and_28_out, and_20_out);
  or or_23 (XM_R2_Bypass, and_29_out, and_21_out);
  or or_24 (MW_R2_Bypass, and_30_out, and_22_out);
  and and_32 (and_32_out, JR_DX, JAL_MW);
  Multiplexer #(.width(32), .enable("false")) multiplexer_21 (
    .in0(multiplexer_20_out), .in1(PC_MW_1), .out(multiplexer_21_out), .sel(and_32_out));
  Multiplexer #(.width(32), .enable("false")) multiplexer_22 (
    .in0(multiplexer_21_out), .in1(data_out_mw), .out(multiplexer_22_out), .sel(and_33_out));
  and and_33 (and_33_out, JR_DX, MW_R1_Bypass);
  and and_34 (and_34_out, Mult_DX, RType_DX);
  and and_35 (and_35_out, Div_DX, RType_DX);
  multdiv multdiv_1 (
    .ctrl_mult(mult_start), .ctrl_div(div_start), .clock(rise), .DataA(real_alu_in1), .DataB(real_alu_in2),
    .data_result(multdiv_result), .data_exception(multdiv_ovf), .data_resultRDY(multdiv_rdy));
  Multiplexer #(.width(32), .enable("false")) multiplexer_23 (
    .in0(Read2_DX), .in1(Read1_DX), .out(multiplexer_23_out), .sel(or_25_out));
  or or_25 (or_25_out, BNE_DX, BLT_DX);
  or or_26 (or_26_out, Addi_DX, SW_DX, LW_DX);
  or or_27 (or_27_out, RType_DX, JR_DX, SW_DX, Addi_DX);
  or or_28 (or_28_out, BNE_DX, BLT_DX);
  and and_36 (and_36_out, JR_DX, XM_R1_Bypass);
  D_Flip_Flop u_Mult_Ongoing (.clk(rise), .D(and_34_out), .Q(Mult_Ongoing_q));  // open: Qn, preset, en, reset
  D_Flip_Flop u_Div_Ongoing (.clk(rise), .D(and_35_out), .Q(Div_Ongoing_q));  // open: Qn, preset, en, reset
  Comparator #(.width(5)) comparator_23 (.a(RS_DX), .b(5'b11110), .eq(comparator_23_eq));  // open: gt, lt
  Comparator #(.width(5)) comparator_24 (.a(RS_DX), .b(5'b11110), .eq(comparator_24_eq));  // open: gt, lt
  Comparator #(.width(5)) comparator_25 (.a(RT_DX), .b(5'b11110), .eq(comparator_25_eq));  // open: gt, lt
  Comparator #(.width(5)) comparator_26 (.a(RT_DX), .b(5'b11110), .eq(comparator_26_eq));  // open: gt, lt
  Comparator #(.width(5)) comparator_27 (.a(RD_DX), .b(5'b11110), .eq(comparator_27_eq));  // open: gt, lt
  or or_29 (or_29_out, BNE_DX, JR_DX, BLT_DX);
  Comparator #(.width(5)) comparator_28 (.a(RD_DX), .b(5'b11110), .eq(comparator_28_eq));  // open: gt, lt
  Comparator #(.width(5)) comparator_29 (.a(RS_DX), .b(5'b11110), .eq(comparator_29_eq));  // open: gt, lt
  Comparator #(.width(5)) comparator_30 (.a(RS_DX), .b(5'b11110), .eq(comparator_30_eq));  // open: gt, lt
  Multiplexer #(.width(32), .enable("false")) multiplexer_24 (
    .in0(multiplexer_22_out), .in1(data_to_write), .out(multiplexer_24_out), .sel(and_36_out));
  not not_10 (not_10_out, Mult_Ongoing_q);
  and and_37 (mult_start, not_10_out, not_12_out, and_34_out);
  not not_11 (not_11_out, Div_Ongoing_q);
  and and_38 (div_start, not_11_out, not_12_out, and_35_out);
  not not_12 (not_12_out, multdiv_rdy);
  Multiplexer #(.width(32), .enable("false")) multiplexer_25 (
    .in0(multiplexer_23_out), .in1(Read1_DX), .out(multiplexer_25_out), .sel(RType_DX));
  Multiplexer #(.width(32), .enable("false")) multiplexer_26 (
    .in0(Read2_DX), .in1(Immediate_32), .out(multiplexer_26_out), .sel(or_26_out));
  Multiplexer #(.width(32), .enable("false")) multiplexer_27 (
    .in0(multiplexer_25_out), .in1(data_out_mw), .out(multiplexer_27_out), .sel(MW_R1_Bypass));
  Multiplexer #(.width(32), .enable("false")) multiplexer_28 (
    .in0(multiplexer_26_out), .in1(data_out_mw), .out(multiplexer_28_out), .sel(MW_R2_Bypass));
  and and_39 (and_39_out, comparator_23_eq, or_27_out, ALU_Ovf_XM);
  and and_40 (and_40_out, comparator_24_eq, or_27_out, ALU_Ovf_MW);
  and and_41 (and_41_out, comparator_25_eq, RType_DX, ALU_Ovf_XM);
  and and_42 (and_42_out, comparator_26_eq, RType_DX, ALU_Ovf_MW);
  and and_43 (and_43_out, comparator_27_eq, ALU_Ovf_XM, or_29_out);
  and and_44 (and_44_out, or_29_out, ALU_Ovf_MW, comparator_28_eq);
  and and_45 (and_45_out, comparator_29_eq, ALU_Ovf_XM, or_28_out);
  and and_46 (and_46_out, or_28_out, ALU_Ovf_MW, comparator_30_eq);
  or or_30 (mult_ongoing, Mult_Ongoing_q, mult_start);
  or or_31 (div_ongoing, Div_Ongoing_q, div_start);
  or or_32 (rstatus_r1_XM_bypass, and_39_out, and_43_out);
  or or_33 (rstatus_r1_MW_bypass, and_40_out, and_44_out);
  or or_34 (rstatus_r2_XM_bypass, and_41_out, and_45_out);
  or or_35 (rstatus_r2_MW_bypass, and_42_out, and_46_out);
  Multiplexer #(.width(32), .enable("false")) multiplexer_29 (
    .in0(multiplexer_27_out), .in1(data_to_write), .out(multiplexer_29_out), .sel(XM_R1_Bypass));
  Multiplexer #(.width(32), .enable("false")) multiplexer_30 (
    .in0(multiplexer_28_out), .in1(data_to_write), .out(multiplexer_30_out), .sel(XM_R2_Bypass));
  Multiplexer #(.enable("false")) multiplexer_31 (
    .in0(ALU_Ovf), .in1(multdiv_ovf), .out(multiplexer_31_out), .sel(multdiv_rdy));
  Multiplexer #(.width(5), .enable("false")) multiplexer_32 (
    .in0(ALUOp), .in1(5'b00001), .out(multiplexer_32_out), .sel(BLT_DX));
  Multiplexer #(.width(32), .enable("false")) multiplexer_33 (
    .in0(ALUOut), .in1(multdiv_result), .out(multiplexer_33_out), .sel(multdiv_rdy));
  Multiplexer #(.width(32), .enable("false")) multiplexer_34 (
    .in0(multiplexer_29_out), .in1(ovf_override_value_2), .out(multiplexer_34_out), .sel(rstatus_r1_MW_bypass));
  Multiplexer #(.width(32), .enable("false")) multiplexer_35 (
    .in0(multiplexer_30_out), .in1(ovf_override_value_2), .out(multiplexer_35_out), .sel(rstatus_r2_MW_bypass));
  or or_36 (or_36_out, Addi_DX, LW_DX, SW_DX);
  Multiplexer #(.width(5), .enable("false")) multiplexer_36 (
    .in0(multiplexer_32_out), .in1({5{1'b0}}), .out(multiplexer_36_out), .sel(or_36_out));
  // XM_Module xm_module_1: pin names not known; wires that end beside it: PC_DX, Read1_DX, multiplexer_33_out, Instr_DX, Target_DX_Extended, multiplexer_31_out, rise, Stall_DX, Global_Reset, XM_RD_IS_0, Instr_XM, RD_XM, PC_XM, Read1_XM, ALUOp_XM, ALU_XM, SetX_XM, Target_XM_Extended, ALU_Ovf_XM, JAL_XM, Opcode_XM, SW_XM, LW_XM, ModifiesRD_XM
  Multiplexer #(.width(32), .enable("false")) multiplexer_37 (
    .in0(multiplexer_34_out), .in1(ovf_override_value), .out(multiplexer_37_out), .sel(rstatus_r1_XM_bypass));
  Multiplexer #(.width(32), .enable("false")) multiplexer_38 (
    .in0(multiplexer_35_out), .in1(ovf_override_value), .out(multiplexer_38_out), .sel(rstatus_r1_XM_bypass));
  Multiplexer #(.select(3), .width(32), .enable("false")) multiplexer_39 (
    .in0(32'h1), .in1(32'h3), .in2({32{1'b0}}), .in3({32{1'b0}}), .in4({32{1'b0}}), .in5({32{1'b0}}),
    .in6(32'h4), .in7(32'h5), .out(multiplexer_39_out), .sel(ALUOp_XM[2:0]));
  Multiplexer #(.select(3), .width(32), .enable("false")) multiplexer_40 (
    .in0(32'h1), .in1(32'h3), .in2({32{1'b0}}), .in3({32{1'b0}}), .in4({32{1'b0}}), .in5({32{1'b0}}),
    .in6(32'h4), .in7(32'h5), .out(multiplexer_40_out), .sel(ALU_Op_MW[2:0]));
  main_alu main_alu_1 (
    .InputA(real_alu_in1), .InputB(real_alu_in2), .shift_amt(Shamt), .opcode(multiplexer_36_out),
    .out_5(ALUOut), .overflow(ALU_Ovf), .isNotEqual(ALU_INE), .isLessThan(ALU_ILT));
  Comparator #(.width(5)) comparator_31 (.a(RD_XM), .b(RD_MW), .eq(comparator_31_eq));  // open: gt, lt
  Comparator #(.width(5)) comparator_32 (.a(Opcode_XM), .b(5'b00101), .eq(comparator_32_eq));  // open: gt, lt
  Comparator #(.width(5)) comparator_33 (.a(OpCode_MW), .b(5'b00101), .eq(comparator_33_eq));  // open: gt, lt
  Multiplexer #(.width(32), .enable("false")) multiplexer_41 (
    .in0(Read1_XM), .in1(final_data_out), .out(multiplexer_41_out), .sel(LW_SW_Bypass));
  and and_47 (LW_SW_Bypass, comparator_31_eq, LW_MW, SW_XM);
  Multiplexer #(.width(32), .enable("false")) multiplexer_42 (
    .in0(multiplexer_37_out), .in1(Target_MW), .out(multiplexer_42_out), .sel(SETX_MW_R1_Bypass));
  Multiplexer #(.width(32), .enable("false")) multiplexer_43 (
    .in0(multiplexer_38_out), .in1(Target_MW), .out(multiplexer_43_out), .sel(SETX_MW_R2_Bypass));
  Multiplexer #(.width(32), .enable("false")) multiplexer_44 (
    .in0(multiplexer_39_out), .in1(32'h2), .out(ovf_override_value), .sel(comparator_32_eq));
  Multiplexer #(.width(32), .enable("false")) multiplexer_45 (
    .in0(multiplexer_40_out), .in1(32'h2), .out(ovf_override_value_2), .sel(comparator_33_eq));
  Multiplexer #(.width(32), .enable("false")) multiplexer_46 (
    .in0(multiplexer_42_out), .in1(Target_XM_Extended), .out(multiplexer_46_out), .sel(SETX_XM_R1_Bypass));
  Multiplexer #(.width(32), .enable("false")) multiplexer_47 (
    .in0(multiplexer_43_out), .in1(Target_XM_Extended), .out(multiplexer_47_out), .sel(SETX_XM_R2_Bypass));
  RAM #(.addrWidth(12), .dataWidth(32), .bus("separate")) ram_1 (
    .addr(ALU_XM[11:0]), .din(multiplexer_41_out), .data(ram_1_data), .str(SW_XM), .clk(rise), .ld(LW_XM));  // open: sel, clr
  Multiplexer #(.width(32), .enable("false")) multiplexer_48 (
    .in0(ALU_XM), .in1(ram_1_data), .out(data_to_write), .sel(LW_XM));
  Multiplexer #(.width(32), .enable("false")) multiplexer_49 (
    .in0(multiplexer_46_out), .in1(PC_MW_1), .out(multiplexer_49_out), .sel(JAL_MW_R1_Bypass));
  Multiplexer #(.width(32), .enable("false")) multiplexer_50 (
    .in0(multiplexer_47_out), .in1(PC_MW_1), .out(multiplexer_50_out), .sel(JAL_MW_R2_Bypass));
  Multiplexer #(.width(32), .enable("false")) multiplexer_51 (
    .in0(multiplexer_49_out), .in1(PC_XM_1), .out(real_alu_in1), .sel(JAL_XM_R1_Bypass));
  Multiplexer #(.width(32), .enable("false")) multiplexer_52 (
    .in0(multiplexer_50_out), .in1(PC_XM_1), .out(real_alu_in2), .sel(JAL_XM_R2_Bypass));
  or or_37 (or_37_out, RType_DX, JR_DX, SW_DX, Addi_DX);
  Multiplexer #(.select(3), .width(32), .enable("false")) multiplexer_53 (
    .in0(32'h1), .in1(32'h3), .in2({32{1'b0}}), .in3({32{1'b0}}), .in4({32{1'b0}}), .in5({32{1'b0}}),
    .in6(32'h4), .in7(32'h5), .out(multiplexer_53_out), .sel(ALU_Op_MW[2:0]));
  Comparator #(.width(5)) comparator_34 (.a(OpCode_MW), .b(5'b00101), .eq(comparator_34_eq));  // open: gt, lt
  Comparator #(.width(5)) comparator_35 (.a(RS_DX), .b({5{1'b1}}), .eq(comparator_35_eq));  // open: gt, lt
  Comparator #(.width(5)) comparator_36 (.a(RD_DX), .b({5{1'b1}}), .eq(comparator_36_eq));  // open: gt, lt
  or or_38 (or_38_out, BNE_DX, BLT_DX);
  Comparator #(.width(5)) comparator_37 (.a(RD_DX), .b({5{1'b1}}), .eq(comparator_37_eq));  // open: gt, lt
  Comparator #(.width(5)) comparator_38 (.a(RS_DX), .b({5{1'b1}}), .eq(comparator_38_eq));  // open: gt, lt
  Comparator #(.width(5)) comparator_39 (.a(RS_DX), .b({5{1'b1}}), .eq(comparator_39_eq));  // open: gt, lt
  MW_Module mw_module_1 (
    .PC(PC_XM), .Stall(Stall_DX), .Clock(rise), .Reset(Global_Reset), .Instruction(Instr_XM),
    .Data_In(data_to_write), .PC_OUT(PC_MW), .Data_to_write(data_out_mw), .Destination_Reg(RD_MW),
    .WEnable(WEn_mw), .Target_In(Target_XM_Extended), .Target_Out(Target_MW), .SetX_MW(SetX_MW),
    .ALUOp(ALU_Op_MW), .LW_MW(LW_MW), .RD_Is_Zero_Register(MW_RD_IS_0), .OpCode(OpCode_MW), .JAL_MW(JAL_MW),
    .ModifiesRD_MW(ModifiesRD_MW));
  Multiplexer #(.width(32), .enable("false")) multiplexer_54 (
    .in0(multiplexer_53_out), .in1(32'h2), .out(multiplexer_54_out), .sel(comparator_34_eq));
  Comparator #(.width(5)) comparator_40 (.a(RS_DX), .b({5{1'b1}}), .eq(comparator_40_eq));  // open: gt, lt
  Comparator #(.width(5)) comparator_41 (.a(RT_DX), .b({5{1'b1}}), .eq(comparator_41_eq));  // open: gt, lt
  Comparator #(.width(5)) comparator_42 (.a(RT_DX), .b({5{1'b1}}), .eq(comparator_42_eq));  // open: gt, lt
  Multiplexer #(.width(32), .enable("false")) multiplexer_55 (
    .in0(data_out_mw), .in1(multiplexer_54_out), .out(final_data_out), .sel(ALU_Ovf_MW));
  and and_48 (and_48_out, comparator_35_eq, or_37_out, JAL_XM);
  and and_49 (and_49_out, comparator_40_eq, or_37_out, JAL_XM);
  and and_50 (and_50_out, comparator_41_eq, RType_DX, JAL_MW);
  and and_51 (and_51_out, comparator_42_eq, RType_DX, JAL_MW);
  and and_52 (and_52_out, comparator_36_eq, JAL_MW, or_38_out);
  and and_53 (and_53_out, or_38_out, JAL_MW, comparator_37_eq);
  and and_54 (and_54_out, comparator_38_eq, JAL_MW, or_38_out);
  and and_55 (and_55_out, or_38_out, JAL_MW, comparator_39_eq);
  Multiplexer #(.width(5), .enable("false")) multiplexer_56 (
    .in0(RD_MW), .in1(5'b11110), .out(final_reg_dest), .sel(ALU_Ovf_MW));
  or or_39 (JAL_XM_R1_Bypass, and_48_out, and_52_out);
  or or_40 (JAL_MW_R1_Bypass, and_49_out, and_53_out);
  or or_41 (JAL_XM_R2_Bypass, and_50_out, and_54_out);
  or or_42 (JAL_MW_R2_Bypass, and_51_out, and_55_out);
  _32_bit_carry_lookahead u_32_bit_carry_lookahead_4 (
    .A_32(PC_MW), .B_32(32'h1), .C0(1'b0), .S(PC_MW_1));  // open: Overflow
  _32_bit_carry_lookahead u_32_bit_carry_lookahead_5 (
    .A_32(PC_XM), .B_32(32'h1), .C0(1'b0), .S(PC_XM_1));  // open: Overflow

  // Other names for the same wires on the sheet: reset = Global_Reset; Stall_MW = Stall_DX; Stall_XM = Stall_DX;
  //   Test[31:0] = {_31_27_OP, _26_22_RD, _21_17_RS, _16_12_RT, _11_7_SHAMT, _6_2_ALUOP, _1_0_ZERO}

  // Notes on the sheet:
  //   contents of rom_1 (hex, n*v repeats v):
  //   28400008 b000000a a8000014 28bc0002 7800000 a800000a b0000064
  //   NOOPs
  //   ByPass for SetX followed by instructions that want to use it
  //   Stall Logic for Mult/Div and JAL
  //   NO-OP for LW Followed Immediately by Rtype/Addi/Branch that Uses Same Destination Reg
  //   PC+1 Calculations for BNE and BLT
  //   ByPass for R Type, LW, SW, and Addi Instructions
  //   Bex ByPass for getting new RStatus
  //   Bypass for JR but JAL hasn't written
  //   RStatus overflow followed 1 or 2 after by an operation that wants to use RStatus
  //   Inputs to send to ALU
  //   LW Followed by SW Bypass
  //   JAL Bypass Calculation, $r31 set but needs to be accessed before being written
  //   Jal PC Calculation
endmodule
